// Logisim project 32_and.circ as structural Verilog: 1 circuit, main circuit AND_32bits
module AND_32bits (
  input  A31,
  input  A30,
  input  A29,
  input  A28,
  input  A27,
  input  A26,
  input  A25,
  input  A24,
  input  A23,
  input  A22,
  input  A21,
  input  A20,
  input  A19,
  input  A18,
  input  A17,
  input  A16,
  input  A15,
  input  A14,
  input  A13,
  input  A12,
  input  A11,
  input  A10,
  input  A9,
  input  A8,
  input  A7,
  input  A6,
  input  A5,
  input  A4,
  input  A3,
  input  A2,
  input  A1,
  input  A0,
  input  B31,
  input  B30,
  input  B29,
  input  B28,
  input  B27,
  input  B26,
  input  B25,
  input  B24,
  input  B23,
  input  B22,
  input  B21,
  input  B20,
  input  B19,
  input  B18,
  input  B17,
  input  B16,
  input  B15,
  input  B14,
  input  B13,
  input  B12,
  input  B11,
  input  B10,
  input  B9,
  input  B8,
  input  B7,
  input  B6,
  input  B5,
  input  B4,
  input  B3,
  input  B2,
  input  B1,
  input  B0,
  output S0,
  output S1,
  output S2,
  output S3,
  output S4,
  output S5,
  output S6,
  output S7,
  output S8,
  output S9,
  output S10,
  output S11,
  output S12,
  output S13,
  output S14,
  output S15,
  output S16,
  output S17,
  output S18,
  output S19,
  output S20,
  output S21,
  output S22,
  output S23,
  output S24,
  output S25,
  output S26,
  output S27,
  output S28,
  output S29,
  output S30,
  output S31
);

  and and_1 (S0, B0, A0);
  and and_2 (S1, B1, A1);
  and and_3 (S2, B2, A2);
  and and_4 (S3, B3, A3);
  and and_5 (S4, B4, A4);
  and and_6 (S5, B5, A5);
  and and_7 (S6, B6, A6);
  and and_8 (S7, B7, A7);
  and and_9 (S8, B8, A8);
  and and_10 (S9, B9, A9);
  and and_11 (S10, B10, A10);
  and and_12 (S11, B11, A11);
  and and_13 (S12, B12, A12);
  and and_14 (S13, B13, A13);
  and and_15 (S14, B14, A14);
  and and_16 (S15, B15, A15);
  and and_17 (S16, B16, A16);
  and and_18 (S17, B17, A17);
  and and_19 (S18, B18, A18);
  and and_20 (S19, B19, A19);
  and and_21 (S20, B20, A20);
  and and_22 (S21, B21, A21);
  and and_23 (S22, B22, A22);
  and and_24 (S23, B23, A23);
  and and_25 (S24, B24, A24);
  and and_26 (S25, B25, A25);
  and and_27 (S26, B26, A26);
  and and_28 (S27, B27, A27);
  and and_29 (S28, B28, A28);
  and and_30 (S29, B29, A29);
  and and_31 (S30, B30, A30);
  and and_32 (S31, B31, A31);
endmodule
