// Logisim project 32_xor_or_and.circ as structural Verilog: 12 circuits, main circuit OR_32Bits
module OR_32Bits (
  input  A31,
  input  A30,
  input  A29,
  input  A28,
  input  A27,
  input  A26,
  input  A25,
  input  A24,
  input  A23,
  input  A22,
  input  A21,
  input  A20,
  input  A19,
  input  A18,
  input  A17,
  input  A16,
  input  A15,
  input  A14,
  input  A13,
  input  A12,
  input  A11,
  input  A10,
  input  A9,
  input  A8,
  input  A7,
  input  A6,
  input  A5,
  input  A4,
  input  A3,
  input  A2,
  input  A1,
  input  A0,
  input  B31,
  input  B30,
  input  B29,
  input  B28,
  input  B27,
  input  B26,
  input  B25,
  input  B24,
  input  B23,
  input  B22,
  input  B21,
  input  B20,
  input  B19,
  input  B18,
  input  B17,
  input  B16,
  input  B15,
  input  B14,
  input  B13,
  input  B12,
  input  B11,
  input  B10,
  input  B9,
  input  B8,
  input  B7,
  input  B6,
  input  B5,
  input  B4,
  input  B3,
  input  B2,
  input  B1,
  input  B0,
  output S0,
  output S1,
  output S2,
  output S3,
  output S4,
  output S5,
  output S6,
  output S7,
  output S8,
  output S9,
  output S10,
  output S11,
  output S12,
  output S13,
  output S14,
  output S15,
  output S16,
  output S17,
  output S18,
  output S19,
  output S20,
  output S21,
  output S22,
  output S23,
  output S24,
  output S25,
  output S26,
  output S27,
  output S28,
  output S29,
  output S30,
  output S31
);

  or or_1 (S0, A0, B0);
  or or_2 (S1, A1, B1);
  or or_3 (S2, A2, B2);
  or or_4 (S3, A3, B3);
  or or_5 (S4, A4, B4);
  or or_6 (S5, A5, B5);
  or or_7 (S6, A6, B6);
  or or_8 (S7, A7, B7);
  or or_9 (S8, A8, B8);
  or or_10 (S9, A9, B9);
  or or_11 (S10, A10, B10);
  or or_12 (S11, A11, B11);
  or or_13 (S12, A12, B12);
  or or_14 (S13, A13, B13);
  or or_15 (S14, A14, B14);
  or or_16 (S15, A15, B15);
  or or_17 (S16, A16, B16);
  or or_18 (S17, A17, B17);
  or or_19 (S18, A18, B18);
  or or_20 (S19, A19, B19);
  or or_21 (S20, A20, B20);
  or or_22 (S21, A21, B21);
  or or_23 (S22, A22, B22);
  or or_24 (S23, A23, B23);
  or or_25 (S24, A24, B24);
  or or_26 (S25, A25, B25);
  or or_27 (S26, A26, B26);
  or or_28 (S27, A27, B27);
  or or_29 (S28, A28, B28);
  or or_30 (S29, A29, B29);
  or or_31 (S30, A30, B30);
  or or_32 (S31, A31, B31);
endmodule

module XOR_32bits (
  input  A31,
  input  A30,
  input  A29,
  input  A28,
  input  A27,
  input  A26,
  input  A25,
  input  A24,
  input  A23,
  input  A22,
  input  A21,
  input  A20,
  input  A19,
  input  A18,
  input  A17,
  input  A16,
  input  A15,
  input  A14,
  input  A13,
  input  A12,
  input  A11,
  input  A10,
  input  A9,
  input  A8,
  input  A7,
  input  A6,
  input  A5,
  input  A4,
  input  A3,
  input  A2,
  input  A1,
  input  A0,
  input  B31,
  input  B30,
  input  B29,
  input  B28,
  input  B27,
  input  B26,
  input  B25,
  input  B24,
  input  B23,
  input  B22,
  input  B21,
  input  B20,
  input  B19,
  input  B18,
  input  B17,
  input  B16,
  input  B15,
  input  B14,
  input  B13,
  input  B12,
  input  B11,
  input  B10,
  input  B9,
  input  B8,
  input  B7,
  input  B6,
  input  B5,
  input  B4,
  input  B3,
  input  B2,
  input  B1,
  input  B0,
  output S0,
  output S1,
  output S2,
  output S3,
  output S4,
  output S5,
  output S6,
  output S7,
  output S8,
  output S9,
  output S10,
  output S11,
  output S12,
  output S13,
  output S14,
  output S15,
  output S16,
  output S17,
  output S18,
  output S19,
  output S20,
  output S21,
  output S22,
  output S23,
  output S24,
  output S25,
  output S26,
  output S27,
  output S28,
  output S29,
  output S30,
  output S31
);

  xor xor_1 (S0, A0, B0);
  xor xor_2 (S1, A1, B1);
  xor xor_3 (S2, A2, B2);
  xor xor_4 (S3, A3, B3);
  xor xor_5 (S4, A4, B4);
  xor xor_6 (S5, A5, B5);
  xor xor_7 (S6, A6, B6);
  xor xor_8 (S7, A7, B7);
  xor xor_9 (S8, A8, B8);
  xor xor_10 (S9, A9, B9);
  xor xor_11 (S10, A10, B10);
  xor xor_12 (S11, A11, B11);
  xor xor_13 (S12, A12, B12);
  xor xor_14 (S13, A13, B13);
  xor xor_15 (S14, A14, B14);
  xor xor_16 (S15, A15, B15);
  xor xor_17 (S16, A16, B16);
  xor xor_18 (S17, A17, B17);
  xor xor_19 (S18, A18, B18);
  xor xor_20 (S19, A19, B19);
  xor xor_21 (S20, A20, B20);
  xor xor_22 (S21, A21, B21);
  xor xor_23 (S22, A22, B22);
  xor xor_24 (S23, A23, B23);
  xor xor_25 (S24, A24, B24);
  xor xor_26 (S25, A25, B25);
  xor xor_27 (S26, A26, B26);
  xor xor_28 (S27, A27, B27);
  xor xor_29 (S28, A28, B28);
  xor xor_30 (S29, A29, B29);
  xor xor_31 (S30, A30, B30);
  xor xor_32 (S31, A31, B31);
endmodule

module AND_32Bits (
  input  A31,
  input  A30,
  input  A29,
  input  A28,
  input  A27,
  input  A26,
  input  A25,
  input  A24,
  input  A23,
  input  A22,
  input  A21,
  input  A20,
  input  A19,
  input  A18,
  input  A17,
  input  A16,
  input  A15,
  input  A14,
  input  A13,
  input  A12,
  input  A11,
  input  A10,
  input  A9,
  input  A8,
  input  A7,
  input  A6,
  input  A5,
  input  A4,
  input  A3,
  input  A2,
  input  A1,
  input  A0,
  input  B31,
  input  B30,
  input  B29,
  input  B28,
  input  B27,
  input  B26,
  input  B25,
  input  B24,
  input  B23,
  input  B22,
  input  B21,
  input  B20,
  input  B19,
  input  B18,
  input  B17,
  input  B16,
  input  B15,
  input  B14,
  input  B13,
  input  B12,
  input  B11,
  input  B10,
  input  B9,
  input  B8,
  input  B7,
  input  B6,
  input  B5,
  input  B4,
  input  B3,
  input  B2,
  input  B1,
  input  B0,
  output S0,
  output S1,
  output S2,
  output S3,
  output S4,
  output S5,
  output S6,
  output S7,
  output S8,
  output S9,
  output S10,
  output S11,
  output S12,
  output S13,
  output S14,
  output S15,
  output S16,
  output S17,
  output S18,
  output S19,
  output S20,
  output S21,
  output S22,
  output S23,
  output S24,
  output S25,
  output S26,
  output S27,
  output S28,
  output S29,
  output S30,
  output S31
);

  and and_1 (S0, A0, B0);
  and and_2 (S1, A1, B1);
  and and_3 (S2, A2, B2);
  and and_4 (S3, A3, B3);
  and and_5 (S4, A4, B4);
  and and_6 (S5, A5, B5);
  and and_7 (S6, A6, B6);
  and and_8 (S7, A7, B7);
  and and_9 (S8, A8, B8);
  and and_10 (S9, A9, B9);
  and and_11 (S10, A10, B10);
  and and_12 (S11, A11, B11);
  and and_13 (S12, A12, B12);
  and and_14 (S13, A13, B13);
  and and_15 (S14, A14, B14);
  and and_16 (S15, A15, B15);
  and and_17 (S16, A16, B16);
  and and_18 (S17, A17, B17);
  and and_19 (S18, A18, B18);
  and and_20 (S19, A19, B19);
  and and_21 (S20, A20, B20);
  and and_22 (S21, A21, B21);
  and and_23 (S22, A22, B22);
  and and_24 (S23, A23, B23);
  and and_25 (S24, A24, B24);
  and and_26 (S25, A25, B25);
  and and_27 (S26, A26, B26);
  and and_28 (S27, A27, B27);
  and and_29 (S28, A28, B28);
  and and_30 (S29, A29, B29);
  and and_31 (S30, A30, B30);
  and and_32 (S31, A31, B31);
endmodule

module mux_1x2 (
  input  A,
  input  B,
  input  S,
  output R
);

  wire and_1_out, and_2_out, not_1_out;

  not not_1 (not_1_out, S);
  and and_1 (and_1_out, A, not_1_out);
  and and_2 (and_2_out, B, S);
  or or_1 (R, and_1_out, and_2_out);
endmodule

module full_adder (
  input  Cin,
  input  A,
  input  B,
  output S
);

  wire xor_1_out;

  xor xor_1 (xor_1_out, A, B);
  xor xor_2 (S, Cin, xor_1_out);
endmodule

module somador_subtrator (
  input  M,
  input  A3,
  input  A2,
  input  A1,
  input  A0,
  input  B3,
  input  B2,
  input  B1,
  input  B0,
  output S3,
  output S2,
  output S1,
  output S0,
  output OVFL,
  output Cout
);

  wire and_1_out, and_2_out, and_3_out, and_4_out, and_5_out, and_6_out, and_7_out, and_8_out, and_9_out,
       and_10_out, G0_out, G1_out, G2_out, G3_out, or_1_out, or_2_out, or_3_out, P0_out, P1_out, P2_out,
       P3_out, xor_1_out, xor_2_out, xor_3_out, xor_4_out;

  xor xor_1 (xor_1_out, M, B3);
  xor xor_2 (xor_2_out, M, B0);
  xor xor_3 (xor_3_out, M, B1);
  xor xor_4 (xor_4_out, M, B2);
  and G1 (G1_out, xor_3_out, A1);
  or P1 (P1_out, xor_3_out, A1);
  and G0 (G0_out, A0, xor_2_out);
  or P0 (P0_out, A0, xor_2_out);
  and G2 (G2_out, xor_4_out, A2);
  or P2 (P2_out, xor_4_out, A2);
  and G3 (G3_out, xor_1_out, A3);
  or P3 (P3_out, xor_1_out, A3);
  and and_1 (and_1_out, P0_out, M);
  and and_2 (and_2_out, G0_out, P1_out);
  and and_3 (and_3_out, P1_out, M, P0_out);
  or or_1 (or_1_out, and_1_out, G0_out);
  and and_4 (and_4_out, G1_out, P2_out);
  and and_5 (and_5_out, P2_out, P1_out, G0_out);
  and and_6 (and_6_out, P2_out, P1_out, P0_out, M);
  and and_7 (and_7_out, P3_out, G2_out);
  and and_8 (and_8_out, P3_out, P2_out, G1_out);
  and and_9 (and_9_out, P3_out, P2_out, P1_out, G0_out);
  and and_10 (and_10_out, P3_out, P2_out, P1_out, P0_out, M);
  or or_2 (or_2_out, G1_out, and_2_out, and_3_out);
  or or_3 (or_3_out, G2_out, and_4_out, and_5_out, and_6_out);
  or or_4 (Cout, G3_out, and_7_out, and_8_out, and_9_out, and_10_out);
  full_adder full_adder_1 (.Cin(M), .A(A0), .B(xor_2_out), .S(S0));
  full_adder full_adder_2 (.Cin(or_1_out), .A(A1), .B(xor_3_out), .S(S1));
  full_adder full_adder_3 (.Cin(or_2_out), .A(A2), .B(xor_4_out), .S(S2));
  full_adder full_adder_4 (.Cin(or_3_out), .A(A3), .B(xor_1_out), .S(S3));
  xor xor_5 (OVFL, or_3_out, Cout);
endmodule

module comparator_1bit (
  input  A,
  input  B,
  output G,
  output E,
  output L
);

  wire not_1_out, not_2_out, or_1_out;

  not not_1 (not_1_out, B);
  not not_2 (not_2_out, A);
  and and_1 (G, A, not_1_out);
  and and_2 (L, not_2_out, B);
  or or_1 (or_1_out, G, L);
  not not_3 (E, or_1_out);
endmodule

module comparator_2btis (
  input  A0,
  input  B0,
  input  A1,
  input  B1,
  output G,
  output E,
  output L
);

  wire and_1_out, comparator_1bit_1_e, comparator_1bit_1_g, comparator_1bit_2_e, comparator_1bit_2_g;

  comparator_1bit comparator_1bit_1 (.A(A0), .B(B0), .G(comparator_1bit_1_g), .E(comparator_1bit_1_e));  // open: L
  comparator_1bit comparator_1bit_2 (.A(A1), .B(B1), .G(comparator_1bit_2_g), .E(comparator_1bit_2_e));  // open: L
  and and_1 (and_1_out, comparator_1bit_1_g, comparator_1bit_2_e);
  or or_1 (G, and_1_out, comparator_1bit_2_g);
  and and_2 (E, comparator_1bit_1_e, comparator_1bit_2_e);
  xnor xnor_1 (L, E, G);
endmodule

module comparator_4bits (
  input  A3,
  input  A2,
  input  A1,
  input  A0,
  input  B3,
  input  B2,
  input  B1,
  input  B0,
  output G,
  output E,
  output L
);

  wire and_1_out, comparator_2btis_1_e, comparator_2btis_1_g, comparator_2btis_2_e, comparator_2btis_2_g;

  comparator_2btis comparator_2btis_1 (
    .G(comparator_2btis_1_g), .E(comparator_2btis_1_e), .B0(B0), .A1(A1), .B1(B1), .A0(A0));  // open: L
  comparator_2btis comparator_2btis_2 (
    .G(comparator_2btis_2_g), .E(comparator_2btis_2_e), .B0(B2), .A1(A3), .B1(B3), .A0(A2));  // open: L
  and and_1 (and_1_out, comparator_2btis_1_g, comparator_2btis_2_e);
  or or_1 (G, and_1_out, comparator_2btis_2_g);
  and and_2 (E, comparator_2btis_1_e, comparator_2btis_2_e);
  xnor xnor_1 (L, E, G);
endmodule

module Tester (
  input  A3,
  input  A2,
  input  A1,
  input  A0,
  input  B3,
  input  B2,
  input  B1,
  input  B0,
  output G,
  output E,
  output L
);

  comparator_4bits comparator_4bits_1 (
    .A3(A3), .A2(A2), .A1(A1), .A0(A0), .B3(B3), .B2(B2), .B1(B1), .B0(B0), .G(G), .E(E), .L(L));
endmodule

module mux_2x4 (
  input  A0,
  input  A1,
  input  A2,
  input  A3,
  input  S1,
  input  S0,
  output X
);

  wire and_1_out, and_2_out, mux_1x2_1_p4, mux_1x2_2_p4, not_1_out;

  // mux_1x2 mux_1x2_1: pin names not known; wires that end beside it: A0, A1, S0, mux_1x2_1_p4
  // mux_1x2 mux_1x2_2: pin names not known; wires that end beside it: A3, A2, S0, mux_1x2_2_p4
  not not_1 (not_1_out, S1);
  and and_1 (and_1_out, mux_1x2_1_p4, not_1_out);
  and and_2 (and_2_out, mux_1x2_2_p4, S1);
  or or_1 (X, and_1_out, and_2_out);
endmodule

module COMPARADOR_32Bits (
  input  A31,
  input  A30,
  input  A29,
  input  A28,
  input  A27,
  input  A26,
  input  A25,
  input  A24,
  input  A23,
  input  A22,
  input  A21,
  input  A20,
  input  A19,
  input  A18,
  input  A17,
  input  A16,
  input  A15,
  input  A14,
  input  A13,
  input  A12,
  input  A11,
  input  A10,
  input  A9,
  input  A8,
  input  A7,
  input  A6,
  input  A5,
  input  A4,
  input  A3,
  input  A2,
  input  A1,
  input  A0,
  input  B31,
  input  B30,
  input  B29,
  input  B28,
  input  B27,
  input  B26,
  input  B25,
  input  B24,
  input  B23,
  input  B22,
  input  B21,
  input  B20,
  input  B19,
  input  B18,
  input  B17,
  input  B16,
  input  B15,
  input  B14,
  input  B13,
  input  B12,
  input  B11,
  input  B10,
  input  B9,
  input  B8,
  input  B7,
  input  B6,
  input  B5,
  input  B4,
  input  B3,
  input  B2,
  input  B1,
  input  B0,
  output E,
  output L,
  output G
);

  wire and_1_out, and_2_out, and_3_out, and_4_out, and_5_out, and_6_out, and_7_out, and_8_out, and_9_out,
       and_10_out, and_11_out, and_12_out, and_13_out, and_14_out, and_15_out, and_16_out, and_17_out,
       and_18_out, and_19_out, and_20_out, and_21_out, and_22_out, and_23_out, and_24_out, and_25_out,
       and_26_out, and_27_out, and_28_out, and_30_out, comparator_2btis_1_e, comparator_2btis_1_g,
       comparator_2btis_2_e, comparator_2btis_2_g, comparator_2btis_3_e, comparator_2btis_3_g,
       comparator_2btis_4_e, comparator_2btis_4_g, comparator_2btis_5_e, comparator_2btis_5_g,
       comparator_2btis_6_e, comparator_2btis_6_g, comparator_2btis_7_e, comparator_2btis_7_g,
       comparator_2btis_8_e, comparator_2btis_8_g, comparator_2btis_9_e, comparator_2btis_9_g,
       comparator_2btis_10_e, comparator_2btis_10_g, comparator_2btis_11_e, comparator_2btis_11_g,
       comparator_2btis_12_e, comparator_2btis_12_g, comparator_2btis_13_e, comparator_2btis_13_g,
       comparator_2btis_14_e, comparator_2btis_14_g, comparator_2btis_15_e, comparator_2btis_15_g,
       comparator_2btis_16_e, comparator_2btis_16_g, or_1_out, or_2_out, or_3_out, or_4_out, or_5_out,
       or_6_out, or_7_out, or_8_out, or_9_out, or_10_out, or_11_out, or_12_out, or_13_out, or_14_out;

  comparator_2btis comparator_2btis_1 (
    .G(comparator_2btis_1_g), .E(comparator_2btis_1_e), .B0(B0), .A1(A1), .B1(B1), .A0(A0));  // open: L
  comparator_2btis comparator_2btis_2 (
    .G(comparator_2btis_2_g), .E(comparator_2btis_2_e), .B0(B2), .A1(A3), .B1(B3), .A0(A2));  // open: L
  comparator_2btis comparator_2btis_3 (
    .G(comparator_2btis_3_g), .E(comparator_2btis_3_e), .B0(B4), .A1(A5), .B1(B5), .A0(A4));  // open: L
  comparator_2btis comparator_2btis_4 (
    .G(comparator_2btis_4_g), .E(comparator_2btis_4_e), .B0(B6), .A1(A7), .B1(B7), .A0(A6));  // open: L
  comparator_2btis comparator_2btis_5 (
    .G(comparator_2btis_5_g), .E(comparator_2btis_5_e), .B0(B8), .A1(A9), .B1(B9), .A0(A8));  // open: L
  comparator_2btis comparator_2btis_6 (
    .G(comparator_2btis_6_g), .E(comparator_2btis_6_e), .B0(B10), .A1(A11), .B1(B11), .A0(A10));  // open: L
  comparator_2btis comparator_2btis_7 (
    .G(comparator_2btis_7_g), .E(comparator_2btis_7_e), .B0(B12), .A1(A13), .B1(B13), .A0(A12));  // open: L
  comparator_2btis comparator_2btis_8 (
    .G(comparator_2btis_8_g), .E(comparator_2btis_8_e), .B0(B14), .A1(A15), .B1(B15), .A0(A14));  // open: L
  comparator_2btis comparator_2btis_9 (
    .G(comparator_2btis_9_g), .E(comparator_2btis_9_e), .B0(B16), .A1(A17), .B1(B17), .A0(A16));  // open: L
  comparator_2btis comparator_2btis_10 (
    .G(comparator_2btis_10_g), .E(comparator_2btis_10_e), .B0(B18), .A1(A19), .B1(B19), .A0(A18));  // open: L
  comparator_2btis comparator_2btis_11 (
    .G(comparator_2btis_11_g), .E(comparator_2btis_11_e), .B0(B20), .A1(A21), .B1(B21), .A0(A20));  // open: L
  comparator_2btis comparator_2btis_12 (
    .G(comparator_2btis_12_g), .E(comparator_2btis_12_e), .B0(B22), .A1(A23), .B1(B23), .A0(A22));  // open: L
  comparator_2btis comparator_2btis_13 (
    .G(comparator_2btis_13_g), .E(comparator_2btis_13_e), .B0(B24), .A1(A25), .B1(B25), .A0(A24));  // open: L
  comparator_2btis comparator_2btis_14 (
    .G(comparator_2btis_14_g), .E(comparator_2btis_14_e), .B0(B26), .A1(A27), .B1(B27), .A0(A26));  // open: L
  comparator_2btis comparator_2btis_15 (
    .G(comparator_2btis_15_g), .E(comparator_2btis_15_e), .B0(B28), .A1(A29), .B1(B29), .A0(A28));  // open: L
  comparator_2btis comparator_2btis_16 (
    .G(comparator_2btis_16_g), .E(comparator_2btis_16_e), .B0(B30), .A1(A31), .B1(B31), .A0(A30));  // open: L
  and and_1 (and_1_out, comparator_2btis_1_e, comparator_2btis_2_e);
  and and_2 (and_2_out, comparator_2btis_1_g, comparator_2btis_2_e);
  and and_3 (and_3_out, comparator_2btis_3_e, comparator_2btis_4_e);
  and and_4 (and_4_out, comparator_2btis_3_g, comparator_2btis_4_e);
  and and_5 (and_5_out, comparator_2btis_5_e, comparator_2btis_6_e);
  and and_6 (and_6_out, comparator_2btis_5_g, comparator_2btis_6_e);
  and and_7 (and_7_out, comparator_2btis_7_e, comparator_2btis_8_e);
  and and_8 (and_8_out, comparator_2btis_7_g, comparator_2btis_8_e);
  and and_9 (and_9_out, comparator_2btis_9_e, comparator_2btis_10_e);
  and and_10 (and_10_out, comparator_2btis_9_g, comparator_2btis_10_e);
  and and_11 (and_11_out, comparator_2btis_11_e, comparator_2btis_12_e);
  and and_12 (and_12_out, comparator_2btis_11_g, comparator_2btis_12_e);
  and and_13 (and_13_out, comparator_2btis_13_e, comparator_2btis_14_e);
  and and_14 (and_14_out, comparator_2btis_13_g, comparator_2btis_14_e);
  and and_15 (and_15_out, comparator_2btis_15_e, comparator_2btis_16_e);
  and and_16 (and_16_out, comparator_2btis_15_g, comparator_2btis_16_e);
  or or_1 (or_1_out, and_2_out, comparator_2btis_2_g);
  or or_2 (or_2_out, and_4_out, comparator_2btis_4_g);
  or or_3 (or_3_out, and_6_out, comparator_2btis_6_g);
  or or_4 (or_4_out, and_8_out, comparator_2btis_8_g);
  or or_5 (or_5_out, and_10_out, comparator_2btis_10_g);
  or or_6 (or_6_out, and_12_out, comparator_2btis_12_g);
  or or_7 (or_7_out, and_14_out, comparator_2btis_14_g);
  or or_8 (or_8_out, and_16_out, comparator_2btis_16_g);
  and and_17 (and_17_out, and_1_out, and_3_out);
  and and_18 (and_18_out, or_1_out, and_3_out);
  and and_19 (and_19_out, and_5_out, and_7_out);
  and and_20 (and_20_out, or_3_out, and_7_out);
  and and_21 (and_21_out, and_9_out, and_11_out);
  and and_22 (and_22_out, or_5_out, and_11_out);
  and and_23 (and_23_out, and_13_out, and_15_out);
  and and_24 (and_24_out, or_7_out, and_15_out);
  or or_9 (or_9_out, and_18_out, or_2_out);
  or or_10 (or_10_out, and_20_out, or_4_out);
  or or_11 (or_11_out, and_22_out, or_6_out);
  or or_12 (or_12_out, and_24_out, or_8_out);
  and and_25 (and_25_out, and_17_out, and_19_out);
  and and_26 (and_26_out, or_9_out, and_19_out);
  and and_27 (and_27_out, and_21_out, and_23_out);
  and and_28 (and_28_out, or_11_out, and_23_out);
  or or_13 (or_13_out, and_26_out, or_10_out);
  or or_14 (or_14_out, and_28_out, or_12_out);
  and and_29 (E, and_25_out, and_27_out);
  and and_30 (and_30_out, or_13_out, and_27_out);
  or or_15 (G, and_30_out, or_14_out);
  nor nor_1 (L, E, G);
endmodule
