// Logisim project ULA.circ as structural Verilog: 18 circuits, main circuit full_adder
module full_adder (
  input  Cin,
  input  A,
  input  B,
  output Cout,
  output S
);

  wire and_1_out, and_2_out, xor_1_out;

  and and_1 (and_1_out, A, B);
  xor xor_1 (xor_1_out, A, B);
  xor xor_2 (S, Cin, xor_1_out);
  and and_2 (and_2_out, Cin, xor_1_out);
  or or_1 (Cout, and_1_out, and_2_out);
endmodule

module somador_subtrator_4bits (
  input  M,
  input  A3,
  input  A2,
  input  A1,
  input  A0,
  input  B3,
  input  B2,
  input  B1,
  input  B0,
  output S3,
  output S2,
  output S1,
  output S0,
  output OVFL,
  output Cout
);

  wire and_1_out, and_2_out, and_3_out, and_4_out, and_5_out, and_6_out, and_7_out, and_8_out, and_9_out,
       and_10_out, G0_out, G1_out, G2_out, G3_out, or_1_out, or_2_out, or_3_out, P0_out, P1_out, P2_out,
       P3_out, xor_1_out, xor_2_out, xor_3_out, xor_4_out;

  xor xor_1 (xor_1_out, M, B3);
  xor xor_2 (xor_2_out, M, B0);
  xor xor_3 (xor_3_out, M, B1);
  xor xor_4 (xor_4_out, M, B2);
  and G1 (G1_out, xor_3_out, A1);
  or P1 (P1_out, xor_3_out, A1);
  and G0 (G0_out, A0, xor_2_out);
  or P0 (P0_out, A0, xor_2_out);
  and G2 (G2_out, xor_4_out, A2);
  or P2 (P2_out, xor_4_out, A2);
  and G3 (G3_out, xor_1_out, A3);
  or P3 (P3_out, xor_1_out, A3);
  and and_1 (and_1_out, P0_out, M);
  and and_2 (and_2_out, G0_out, P1_out);
  and and_3 (and_3_out, P1_out, M, P0_out);
  or or_1 (or_1_out, and_1_out, G0_out);
  and and_4 (and_4_out, G1_out, P2_out);
  and and_5 (and_5_out, P2_out, P1_out, G0_out);
  and and_6 (and_6_out, P2_out, P1_out, P0_out, M);
  and and_7 (and_7_out, P3_out, G2_out);
  and and_8 (and_8_out, P3_out, P2_out, G1_out);
  and and_9 (and_9_out, P3_out, P2_out, P1_out, G0_out);
  and and_10 (and_10_out, P3_out, P2_out, P1_out, P0_out, M);
  or or_2 (or_2_out, G1_out, and_2_out, and_3_out);
  or or_3 (or_3_out, G2_out, and_4_out, and_5_out, and_6_out);
  or or_4 (Cout, G3_out, and_7_out, and_8_out, and_9_out, and_10_out);
  full_adder full_adder_1 (.Cin(M), .A(A0), .B(xor_2_out), .S(S0));  // open: Cout
  full_adder full_adder_2 (.Cin(or_1_out), .A(A1), .B(xor_3_out), .S(S1));  // open: Cout
  full_adder full_adder_3 (.Cin(or_2_out), .A(A2), .B(xor_4_out), .S(S2));  // open: Cout
  full_adder full_adder_4 (.Cin(or_3_out), .A(A3), .B(xor_1_out), .S(S3));  // open: Cout
  xor xor_5 (OVFL, or_3_out, Cout);
endmodule

module OR_32Bits (
  input  A31,
  input  A30,
  input  A29,
  input  A28,
  input  A27,
  input  A26,
  input  A25,
  input  A24,
  input  A23,
  input  A22,
  input  A21,
  input  A20,
  input  A19,
  input  A18,
  input  A17,
  input  A16,
  input  A15,
  input  A14,
  input  A13,
  input  A12,
  input  A11,
  input  A10,
  input  A9,
  input  A8,
  input  A7,
  input  A6,
  input  A5,
  input  A4,
  input  A3,
  input  A2,
  input  A1,
  input  A0,
  input  B31,
  input  B30,
  input  B29,
  input  B28,
  input  B27,
  input  B26,
  input  B25,
  input  B24,
  input  B23,
  input  B22,
  input  B21,
  input  B20,
  input  B19,
  input  B18,
  input  B17,
  input  B16,
  input  B15,
  input  B14,
  input  B13,
  input  B12,
  input  B11,
  input  B10,
  input  B9,
  input  B8,
  input  B7,
  input  B6,
  input  B5,
  input  B4,
  input  B3,
  input  B2,
  input  B1,
  input  B0,
  output S0,
  output S1,
  output S2,
  output S3,
  output S4,
  output S5,
  output S6,
  output S7,
  output S8,
  output S9,
  output S10,
  output S11,
  output S12,
  output S13,
  output S14,
  output S15,
  output S16,
  output S17,
  output S18,
  output S19,
  output S20,
  output S21,
  output S22,
  output S23,
  output S24,
  output S25,
  output S26,
  output S27,
  output S28,
  output S29,
  output S30,
  output S31
);

  or or_1 (S0, A0, B0);
  or or_2 (S1, A1, B1);
  or or_3 (S2, A2, B2);
  or or_4 (S3, A3, B3);
  or or_5 (S4, A4, B4);
  or or_6 (S5, A5, B5);
  or or_7 (S6, A6, B6);
  or or_8 (S7, A7, B7);
  or or_9 (S8, A8, B8);
  or or_10 (S9, A9, B9);
  or or_11 (S10, A10, B10);
  or or_12 (S11, A11, B11);
  or or_13 (S12, A12, B12);
  or or_14 (S13, A13, B13);
  or or_15 (S14, A14, B14);
  or or_16 (S15, A15, B15);
  or or_17 (S16, A16, B16);
  or or_18 (S17, A17, B17);
  or or_19 (S18, A18, B18);
  or or_20 (S19, A19, B19);
  or or_21 (S20, A20, B20);
  or or_22 (S21, A21, B21);
  or or_23 (S22, A22, B22);
  or or_24 (S23, A23, B23);
  or or_25 (S24, A24, B24);
  or or_26 (S25, A25, B25);
  or or_27 (S26, A26, B26);
  or or_28 (S27, A27, B27);
  or or_29 (S28, A28, B28);
  or or_30 (S29, A29, B29);
  or or_31 (S30, A30, B30);
  or or_32 (S31, A31, B31);
endmodule

module XOR_32bits (
  input  A31,
  input  A30,
  input  A29,
  input  A28,
  input  A27,
  input  A26,
  input  A25,
  input  A24,
  input  A23,
  input  A22,
  input  A21,
  input  A20,
  input  A19,
  input  A18,
  input  A17,
  input  A16,
  input  A15,
  input  A14,
  input  A13,
  input  A12,
  input  A11,
  input  A10,
  input  A9,
  input  A8,
  input  A7,
  input  A6,
  input  A5,
  input  A4,
  input  A3,
  input  A2,
  input  A1,
  input  A0,
  input  B31,
  input  B30,
  input  B29,
  input  B28,
  input  B27,
  input  B26,
  input  B25,
  input  B24,
  input  B23,
  input  B22,
  input  B21,
  input  B20,
  input  B19,
  input  B18,
  input  B17,
  input  B16,
  input  B15,
  input  B14,
  input  B13,
  input  B12,
  input  B11,
  input  B10,
  input  B9,
  input  B8,
  input  B7,
  input  B6,
  input  B5,
  input  B4,
  input  B3,
  input  B2,
  input  B1,
  input  B0,
  output S0,
  output S1,
  output S2,
  output S3,
  output S4,
  output S5,
  output S6,
  output S7,
  output S8,
  output S9,
  output S10,
  output S11,
  output S12,
  output S13,
  output S14,
  output S15,
  output S16,
  output S17,
  output S18,
  output S19,
  output S20,
  output S21,
  output S22,
  output S23,
  output S24,
  output S25,
  output S26,
  output S27,
  output S28,
  output S29,
  output S30,
  output S31
);

  xor xor_1 (S0, A0, B0);
  xor xor_2 (S1, A1, B1);
  xor xor_3 (S2, A2, B2);
  xor xor_4 (S3, A3, B3);
  xor xor_5 (S4, A4, B4);
  xor xor_6 (S5, A5, B5);
  xor xor_7 (S6, A6, B6);
  xor xor_8 (S7, A7, B7);
  xor xor_9 (S8, A8, B8);
  xor xor_10 (S9, A9, B9);
  xor xor_11 (S10, A10, B10);
  xor xor_12 (S11, A11, B11);
  xor xor_13 (S12, A12, B12);
  xor xor_14 (S13, A13, B13);
  xor xor_15 (S14, A14, B14);
  xor xor_16 (S15, A15, B15);
  xor xor_17 (S16, A16, B16);
  xor xor_18 (S17, A17, B17);
  xor xor_19 (S18, A18, B18);
  xor xor_20 (S19, A19, B19);
  xor xor_21 (S20, A20, B20);
  xor xor_22 (S21, A21, B21);
  xor xor_23 (S22, A22, B22);
  xor xor_24 (S23, A23, B23);
  xor xor_25 (S24, A24, B24);
  xor xor_26 (S25, A25, B25);
  xor xor_27 (S26, A26, B26);
  xor xor_28 (S27, A27, B27);
  xor xor_29 (S28, A28, B28);
  xor xor_30 (S29, A29, B29);
  xor xor_31 (S30, A30, B30);
  xor xor_32 (S31, A31, B31);
endmodule

module AND_32Bits (
  input  A31,
  input  A30,
  input  A29,
  input  A28,
  input  A27,
  input  A26,
  input  A25,
  input  A24,
  input  A23,
  input  A22,
  input  A21,
  input  A20,
  input  A19,
  input  A18,
  input  A17,
  input  A16,
  input  A15,
  input  A14,
  input  A13,
  input  A12,
  input  A11,
  input  A10,
  input  A9,
  input  A8,
  input  A7,
  input  A6,
  input  A5,
  input  A4,
  input  A3,
  input  A2,
  input  A1,
  input  A0,
  input  B31,
  input  B30,
  input  B29,
  input  B28,
  input  B27,
  input  B26,
  input  B25,
  input  B24,
  input  B23,
  input  B22,
  input  B21,
  input  B20,
  input  B19,
  input  B18,
  input  B17,
  input  B16,
  input  B15,
  input  B14,
  input  B13,
  input  B12,
  input  B11,
  input  B10,
  input  B9,
  input  B8,
  input  B7,
  input  B6,
  input  B5,
  input  B4,
  input  B3,
  input  B2,
  input  B1,
  input  B0,
  output S0,
  output S1,
  output S2,
  output S3,
  output S4,
  output S5,
  output S6,
  output S7,
  output S8,
  output S9,
  output S10,
  output S11,
  output S12,
  output S13,
  output S14,
  output S15,
  output S16,
  output S17,
  output S18,
  output S19,
  output S20,
  output S21,
  output S22,
  output S23,
  output S24,
  output S25,
  output S26,
  output S27,
  output S28,
  output S29,
  output S30,
  output S31
);

  and and_1 (S0, A0, B0);
  and and_2 (S1, A1, B1);
  and and_3 (S2, A2, B2);
  and and_4 (S3, A3, B3);
  and and_5 (S4, A4, B4);
  and and_6 (S5, A5, B5);
  and and_7 (S6, A6, B6);
  and and_8 (S7, A7, B7);
  and and_9 (S8, A8, B8);
  and and_10 (S9, A9, B9);
  and and_11 (S10, A10, B10);
  and and_12 (S11, A11, B11);
  and and_13 (S12, A12, B12);
  and and_14 (S13, A13, B13);
  and and_15 (S14, A14, B14);
  and and_16 (S15, A15, B15);
  and and_17 (S16, A16, B16);
  and and_18 (S17, A17, B17);
  and and_19 (S18, A18, B18);
  and and_20 (S19, A19, B19);
  and and_21 (S20, A20, B20);
  and and_22 (S21, A21, B21);
  and and_23 (S22, A22, B22);
  and and_24 (S23, A23, B23);
  and and_25 (S24, A24, B24);
  and and_26 (S25, A25, B25);
  and and_27 (S26, A26, B26);
  and and_28 (S27, A27, B27);
  and and_29 (S28, A28, B28);
  and and_30 (S29, A29, B29);
  and and_31 (S30, A30, B30);
  and and_32 (S31, A31, B31);
endmodule

module mux_1x2 (
  input  A,
  input  B,
  input  S,
  output R
);

  wire and_1_out, and_2_out, not_1_out;

  not not_1 (not_1_out, S);
  and and_1 (and_1_out, A, not_1_out);
  and and_2 (and_2_out, B, S);
  or or_1 (R, and_1_out, and_2_out);
endmodule

module comparator_1bit (
  input  A,
  input  B,
  output G,
  output E,
  output L
);

  wire not_1_out, not_2_out, or_1_out;

  not not_1 (not_1_out, B);
  not not_2 (not_2_out, A);
  and and_1 (G, A, not_1_out);
  and and_2 (L, not_2_out, B);
  or or_1 (or_1_out, G, L);
  not not_3 (E, or_1_out);
endmodule

module comparator_2btis (
  input  A0,
  input  B0,
  input  A1,
  input  B1,
  output G,
  output E,
  output L
);

  wire and_1_out, comparator_1bit_1_e, comparator_1bit_1_g, comparator_1bit_2_e, comparator_1bit_2_g;

  comparator_1bit comparator_1bit_1 (.A(A0), .B(B0), .G(comparator_1bit_1_g), .E(comparator_1bit_1_e));  // open: L
  comparator_1bit comparator_1bit_2 (.A(A1), .B(B1), .G(comparator_1bit_2_g), .E(comparator_1bit_2_e));  // open: L
  and and_1 (and_1_out, comparator_1bit_1_g, comparator_1bit_2_e);
  or or_1 (G, and_1_out, comparator_1bit_2_g);
  and and_2 (E, comparator_1bit_1_e, comparator_1bit_2_e);
  xnor xnor_1 (L, E, G);
endmodule

module comparator_4bits (
  input  A3,
  input  A2,
  input  A1,
  input  A0,
  input  B3,
  input  B2,
  input  B1,
  input  B0,
  output G,
  output E,
  output L
);

  wire and_1_out, comparator_2btis_1_e, comparator_2btis_1_g, comparator_2btis_2_e, comparator_2btis_2_g;

  comparator_2btis comparator_2btis_1 (
    .A0(A0), .B0(A1), .A1(B0), .B1(B1), .G(comparator_2btis_1_g), .E(comparator_2btis_1_e));  // open: L
  comparator_2btis comparator_2btis_2 (
    .A0(A2), .B0(A3), .A1(B2), .B1(B3), .G(comparator_2btis_2_g), .E(comparator_2btis_2_e));  // open: L
  and and_1 (and_1_out, comparator_2btis_1_g, comparator_2btis_2_e);
  or or_1 (G, and_1_out, comparator_2btis_2_g);
  and and_2 (E, comparator_2btis_1_e, comparator_2btis_2_e);
  xnor xnor_1 (L, E, G);
endmodule

module Tester (
  input  A3,
  input  A2,
  input  A1,
  input  A0,
  input  B3,
  input  B2,
  input  B1,
  input  B0,
  output G,
  output E,
  output L
);

  comparator_4bits comparator_4bits_1 (
    .A3(A3), .A2(A2), .A1(A1), .A0(A0), .B3(B3), .B2(B2), .B1(B1), .B0(B0), .G(G), .E(E), .L(L));
endmodule

module mux_2x4 (
  input  A0,
  input  A1,
  input  A2,
  input  A3,
  input  S1,
  input  S0,
  output X
);

  wire and_1_out, and_2_out, mux_1x2_1_r, mux_1x2_2_r, not_1_out;

  mux_1x2 mux_1x2_1 (.A(A0), .B(A1), .S(S0), .R(mux_1x2_1_r));
  mux_1x2 mux_1x2_2 (.A(A2), .B(A3), .S(S0), .R(mux_1x2_2_r));
  not not_1 (not_1_out, S1);
  and and_1 (and_1_out, mux_1x2_1_r, not_1_out);
  and and_2 (and_2_out, mux_1x2_2_r, S1);
  or or_1 (X, and_1_out, and_2_out);
endmodule

module COMPARADOR_32Bits (
  input  A31,
  input  A30,
  input  A29,
  input  A28,
  input  A27,
  input  A26,
  input  A25,
  input  A24,
  input  A23,
  input  A22,
  input  A21,
  input  A20,
  input  A19,
  input  A18,
  input  A17,
  input  A16,
  input  A15,
  input  A14,
  input  A13,
  input  A12,
  input  A11,
  input  A10,
  input  A9,
  input  A8,
  input  A7,
  input  A6,
  input  A5,
  input  A4,
  input  A3,
  input  A2,
  input  A1,
  input  A0,
  input  B31,
  input  B30,
  input  B29,
  input  B28,
  input  B27,
  input  B26,
  input  B25,
  input  B24,
  input  B23,
  input  B22,
  input  B21,
  input  B20,
  input  B19,
  input  B18,
  input  B17,
  input  B16,
  input  B15,
  input  B14,
  input  B13,
  input  B12,
  input  B11,
  input  B10,
  input  B9,
  input  B8,
  input  B7,
  input  B6,
  input  B5,
  input  B4,
  input  B3,
  input  B2,
  input  B1,
  input  B0,
  output E,
  output L,
  output G
);

  wire and_1_out, and_2_out, and_3_out, and_4_out, and_5_out, and_6_out, and_7_out, and_8_out, and_9_out,
       and_10_out, and_11_out, and_12_out, and_13_out, and_14_out, and_15_out, and_16_out, and_17_out,
       and_18_out, and_19_out, and_20_out, and_21_out, and_22_out, and_23_out, and_24_out, and_25_out,
       and_26_out, and_27_out, and_28_out, and_30_out, comparator_2btis_1_e, comparator_2btis_1_g,
       comparator_2btis_2_e, comparator_2btis_2_g, comparator_2btis_3_e, comparator_2btis_3_g,
       comparator_2btis_4_e, comparator_2btis_4_g, comparator_2btis_5_e, comparator_2btis_5_g,
       comparator_2btis_6_e, comparator_2btis_6_g, comparator_2btis_7_e, comparator_2btis_7_g,
       comparator_2btis_8_e, comparator_2btis_8_g, comparator_2btis_9_e, comparator_2btis_9_g,
       comparator_2btis_10_e, comparator_2btis_10_g, comparator_2btis_11_e, comparator_2btis_11_g,
       comparator_2btis_12_e, comparator_2btis_12_g, comparator_2btis_13_e, comparator_2btis_13_g,
       comparator_2btis_14_e, comparator_2btis_14_g, comparator_2btis_15_e, comparator_2btis_15_g,
       comparator_2btis_16_e, comparator_2btis_16_g, or_1_out, or_2_out, or_3_out, or_4_out, or_5_out,
       or_6_out, or_7_out, or_8_out, or_9_out, or_10_out, or_11_out, or_12_out, or_13_out, or_14_out;

  comparator_2btis comparator_2btis_1 (
    .A0(A0), .B0(A1), .A1(B0), .B1(B1), .G(comparator_2btis_1_g), .E(comparator_2btis_1_e));  // open: L
  comparator_2btis comparator_2btis_2 (
    .A0(A2), .B0(A3), .A1(B2), .B1(B3), .G(comparator_2btis_2_g), .E(comparator_2btis_2_e));  // open: L
  comparator_2btis comparator_2btis_3 (
    .A0(A4), .B0(A5), .A1(B4), .B1(B5), .G(comparator_2btis_3_g), .E(comparator_2btis_3_e));  // open: L
  comparator_2btis comparator_2btis_4 (
    .A0(A6), .B0(A7), .A1(B6), .B1(B7), .G(comparator_2btis_4_g), .E(comparator_2btis_4_e));  // open: L
  comparator_2btis comparator_2btis_5 (
    .A0(A8), .B0(A9), .A1(B8), .B1(B9), .G(comparator_2btis_5_g), .E(comparator_2btis_5_e));  // open: L
  comparator_2btis comparator_2btis_6 (
    .A0(A10), .B0(A11), .A1(B10), .B1(B11), .G(comparator_2btis_6_g), .E(comparator_2btis_6_e));  // open: L
  comparator_2btis comparator_2btis_7 (
    .A0(A12), .B0(A13), .A1(B12), .B1(B13), .G(comparator_2btis_7_g), .E(comparator_2btis_7_e));  // open: L
  comparator_2btis comparator_2btis_8 (
    .A0(A14), .B0(A15), .A1(B14), .B1(B15), .G(comparator_2btis_8_g), .E(comparator_2btis_8_e));  // open: L
  comparator_2btis comparator_2btis_9 (
    .A0(A16), .B0(A17), .A1(B16), .B1(B17), .G(comparator_2btis_9_g), .E(comparator_2btis_9_e));  // open: L
  comparator_2btis comparator_2btis_10 (
    .A0(A18), .B0(A19), .A1(B18), .B1(B19), .G(comparator_2btis_10_g), .E(comparator_2btis_10_e));  // open: L
  comparator_2btis comparator_2btis_11 (
    .A0(A20), .B0(A21), .A1(B20), .B1(B21), .G(comparator_2btis_11_g), .E(comparator_2btis_11_e));  // open: L
  comparator_2btis comparator_2btis_12 (
    .A0(A22), .B0(A23), .A1(B22), .B1(B23), .G(comparator_2btis_12_g), .E(comparator_2btis_12_e));  // open: L
  comparator_2btis comparator_2btis_13 (
    .A0(A24), .B0(A25), .A1(B24), .B1(B25), .G(comparator_2btis_13_g), .E(comparator_2btis_13_e));  // open: L
  comparator_2btis comparator_2btis_14 (
    .A0(A26), .B0(A27), .A1(B26), .B1(B27), .G(comparator_2btis_14_g), .E(comparator_2btis_14_e));  // open: L
  comparator_2btis comparator_2btis_15 (
    .A0(A28), .B0(A29), .A1(B28), .B1(B29), .G(comparator_2btis_15_g), .E(comparator_2btis_15_e));  // open: L
  comparator_2btis comparator_2btis_16 (
    .A0(A30), .B0(A31), .A1(B30), .B1(B31), .G(comparator_2btis_16_g), .E(comparator_2btis_16_e));  // open: L
  and and_1 (and_1_out, comparator_2btis_1_e, comparator_2btis_2_e);
  and and_2 (and_2_out, comparator_2btis_1_g, comparator_2btis_2_e);
  and and_3 (and_3_out, comparator_2btis_3_e, comparator_2btis_4_e);
  and and_4 (and_4_out, comparator_2btis_3_g, comparator_2btis_4_e);
  and and_5 (and_5_out, comparator_2btis_5_e, comparator_2btis_6_e);
  and and_6 (and_6_out, comparator_2btis_5_g, comparator_2btis_6_e);
  and and_7 (and_7_out, comparator_2btis_7_e, comparator_2btis_8_e);
  and and_8 (and_8_out, comparator_2btis_7_g, comparator_2btis_8_e);
  and and_9 (and_9_out, comparator_2btis_9_e, comparator_2btis_10_e);
  and and_10 (and_10_out, comparator_2btis_9_g, comparator_2btis_10_e);
  and and_11 (and_11_out, comparator_2btis_11_e, comparator_2btis_12_e);
  and and_12 (and_12_out, comparator_2btis_11_g, comparator_2btis_12_e);
  and and_13 (and_13_out, comparator_2btis_13_e, comparator_2btis_14_e);
  and and_14 (and_14_out, comparator_2btis_13_g, comparator_2btis_14_e);
  and and_15 (and_15_out, comparator_2btis_15_e, comparator_2btis_16_e);
  and and_16 (and_16_out, comparator_2btis_15_g, comparator_2btis_16_e);
  or or_1 (or_1_out, and_2_out, comparator_2btis_2_g);
  or or_2 (or_2_out, and_4_out, comparator_2btis_4_g);
  or or_3 (or_3_out, and_6_out, comparator_2btis_6_g);
  or or_4 (or_4_out, and_8_out, comparator_2btis_8_g);
  or or_5 (or_5_out, and_10_out, comparator_2btis_10_g);
  or or_6 (or_6_out, and_12_out, comparator_2btis_12_g);
  or or_7 (or_7_out, and_14_out, comparator_2btis_14_g);
  or or_8 (or_8_out, and_16_out, comparator_2btis_16_g);
  and and_17 (and_17_out, and_1_out, and_3_out);
  and and_18 (and_18_out, or_1_out, and_3_out);
  and and_19 (and_19_out, and_5_out, and_7_out);
  and and_20 (and_20_out, or_3_out, and_7_out);
  and and_21 (and_21_out, and_9_out, and_11_out);
  and and_22 (and_22_out, or_5_out, and_11_out);
  and and_23 (and_23_out, and_13_out, and_15_out);
  and and_24 (and_24_out, or_7_out, and_15_out);
  or or_9 (or_9_out, and_18_out, or_2_out);
  or or_10 (or_10_out, and_20_out, or_4_out);
  or or_11 (or_11_out, and_22_out, or_6_out);
  or or_12 (or_12_out, and_24_out, or_8_out);
  and and_25 (and_25_out, and_17_out, and_19_out);
  and and_26 (and_26_out, or_9_out, and_19_out);
  and and_27 (and_27_out, and_21_out, and_23_out);
  and and_28 (and_28_out, or_11_out, and_23_out);
  or or_13 (or_13_out, and_26_out, or_10_out);
  or or_14 (or_14_out, and_28_out, or_12_out);
  and and_29 (E, and_25_out, and_27_out);
  and and_30 (and_30_out, or_13_out, and_27_out);
  or or_15 (G, and_30_out, or_14_out);
  nor nor_1 (L, E, G);
endmodule

module SOMADOR_32bits (
  input  A31,
  input  A30,
  input  A29,
  input  A28,
  input  A27,
  input  A26,
  input  A25,
  input  A24,
  input  A23,
  input  A22,
  input  A21,
  input  A20,
  input  A19,
  input  A18,
  input  A17,
  input  A16,
  input  A15,
  input  A14,
  input  A13,
  input  A12,
  input  A11,
  input  A10,
  input  A9,
  input  A8,
  input  A7,
  input  A6,
  input  A5,
  input  A4,
  input  A3,
  input  A2,
  input  A1,
  input  A0,
  input  M,
  input  B31,
  input  B30,
  input  B29,
  input  B28,
  input  B27,
  input  B26,
  input  B25,
  input  B24,
  input  B23,
  input  B22,
  input  B21,
  input  B20,
  input  B19,
  input  B18,
  input  B17,
  input  B16,
  input  B15,
  input  B14,
  input  B13,
  input  B12,
  input  B11,
  input  B10,
  input  B9,
  input  B8,
  input  B7,
  input  B6,
  input  B5,
  input  B4,
  input  B3,
  input  B2,
  input  B1,
  input  B0,
  output S0,
  output S1,
  output S2,
  output S3,
  output S4,
  output S5,
  output S6,
  output S7,
  output S8,
  output S9,
  output S10,
  output S11,
  output S12,
  output S13,
  output S14,
  output S15,
  output S16,
  output S17,
  output S18,
  output S19,
  output S20,
  output S21,
  output S22,
  output S23,
  output S24,
  output S25,
  output S26,
  output S27,
  output S28,
  output S29,
  output S30,
  output S31,
  output Cout,
  output OVFL
);

  wire add_4bits_1_cout, add_4bits_2_cout, add_4bits_3_cout, add_4bits_4_cout, add_4bits_5_cout,
       add_4bits_6_cout;

  add_4bits add_4bits_1 (
    .S3(S3), .Cout(add_4bits_1_cout), .S2(S2), .S0(S0), .S1(S1), .A3(A3), .A2(A2), .B3(B31), .A1(A1),
    .B2(B30), .B1(B29), .A0(A0), .B0(B28), .M(M));
  add_4bits add_4bits_2 (
    .S3(S7), .Cout(add_4bits_2_cout), .S2(S6), .S0(S4), .S1(S5), .A3(A7), .A2(A6), .B3(B27), .A1(A5),
    .B2(B26), .B1(B25), .A0(A4), .B0(B24), .M(add_4bits_1_cout));
  add_4bits add_4bits_3 (
    .S3(S11), .Cout(add_4bits_3_cout), .S2(S10), .S0(S8), .S1(S9), .A3(A11), .A2(A10), .B3(B23), .A1(A9),
    .B2(B22), .B1(B21), .A0(A8), .B0(B20), .M(add_4bits_2_cout));
  add_4bits add_4bits_4 (
    .S3(S15), .Cout(add_4bits_4_cout), .S2(S14), .S0(S12), .S1(S13), .A3(A15), .A2(A14), .B3(B19), .A1(A13),
    .B2(B18), .B1(B17), .A0(A12), .B0(B16), .M(add_4bits_3_cout));
  add_4bits add_4bits_5 (
    .S3(S19), .Cout(add_4bits_5_cout), .S2(S18), .S0(S16), .S1(S17), .A3(A19), .A2(A18), .B3(B15), .A1(A17),
    .B2(B14), .B1(B13), .A0(A16), .B0(B12), .M(add_4bits_4_cout));
  add_4bits add_4bits_6 (
    .S3(S23), .Cout(add_4bits_6_cout), .S2(S22), .S0(S20), .S1(S21), .A3(A23), .A2(A22), .B3(B11), .A1(A21),
    .B2(B10), .B1(B9), .A0(A20), .B0(B8), .M(add_4bits_5_cout));
  add_4bits add_4bits_7 (
    .S3(S27), .Cout(OVFL), .S2(S26), .S0(S24), .S1(S25), .A3(A27), .A2(A26), .B3(B7), .A1(A25), .B2(B6),
    .B1(B5), .A0(A24), .B0(B4), .M(add_4bits_6_cout));
  add_4bits add_4bits_8 (
    .S3(S31), .Cout(Cout), .S2(S30), .S0(S28), .S1(S29), .A3(A31), .A2(A30), .B3(B3), .A1(A29), .B2(B2),
    .B1(B1), .A0(A28), .B0(B0), .M(OVFL));
endmodule

module add_4bits (
  input  A3,
  input  A2,
  input  A1,
  input  A0,
  input  M,
  input  B3,
  input  B2,
  input  B1,
  input  B0,
  output S0,
  output S1,
  output S2,
  output S3,
  output Cout
);

  wire full_adder_1_cout, full_adder_2_cout, full_adder_3_cout;

  full_adder full_adder_1 (.Cin(M), .A(A0), .B(B0), .Cout(full_adder_1_cout), .S(S0));
  full_adder full_adder_2 (.Cin(full_adder_1_cout), .A(A1), .B(B1), .Cout(full_adder_2_cout), .S(S1));
  full_adder full_adder_3 (.Cin(full_adder_2_cout), .A(A2), .B(B2), .Cout(full_adder_3_cout), .S(S2));
  full_adder full_adder_4 (.Cin(full_adder_3_cout), .A(A3), .B(B3), .Cout(Cout), .S(S3));
endmodule

module sum_sa (
  input  A31,
  input  A30,
  input  A29,
  input  A28,
  input  A27,
  input  A26,
  input  A25,
  input  A24,
  input  A23,
  input  A22,
  input  A21,
  input  A20,
  input  A19,
  input  A18,
  input  A17,
  input  A16,
  input  A15,
  input  A14,
  input  A13,
  input  A12,
  input  A11,
  input  A10,
  input  A9,
  input  A8,
  input  A7,
  input  A6,
  input  A5,
  input  A4,
  input  A3,
  input  A2,
  input  A1,
  input  A0,
  input  Sa,
  output S0,
  output S1,
  output S2,
  output S3,
  output S4,
  output S5,
  output S6,
  output S7,
  output S8,
  output S9,
  output S10,
  output S11,
  output S12,
  output S13,
  output S14,
  output S15,
  output S16,
  output S17,
  output S18,
  output S19,
  output S20,
  output S21,
  output S22,
  output S23,
  output S24,
  output S25,
  output S26,
  output S27,
  output S28,
  output S29,
  output S30,
  output S31
);

  wire not_1_out;

  not not_1 (not_1_out, Sa);
  and and_1 (S0, A0, not_1_out);
  and and_2 (S1, A1, not_1_out);
  and and_3 (S2, A2, not_1_out);
  and and_4 (S3, A3, not_1_out);
  and and_5 (S4, A4, not_1_out);
  and and_6 (S5, A5, not_1_out);
  and and_7 (S6, A6, not_1_out);
  and and_8 (S7, A7, not_1_out);
  and and_9 (S8, A8, not_1_out);
  and and_10 (S9, A9, not_1_out);
  and and_11 (S10, A10, not_1_out);
  and and_12 (S11, A11, not_1_out);
  and and_13 (S12, A12, not_1_out);
  and and_14 (S13, A13, not_1_out);
  and and_15 (S14, A14, not_1_out);
  and and_16 (S15, A15, not_1_out);
  and and_17 (S16, A16, not_1_out);
  and and_18 (S17, A17, not_1_out);
  and and_19 (S18, A18, not_1_out);
  and and_20 (S19, A19, not_1_out);
  and and_21 (S20, A20, not_1_out);
  and and_22 (S21, A21, not_1_out);
  and and_23 (S22, A22, not_1_out);
  and and_24 (S23, A23, not_1_out);
  and and_25 (S24, A24, not_1_out);
  and and_26 (S25, A25, not_1_out);
  and and_27 (S26, A26, not_1_out);
  and and_28 (S27, A27, not_1_out);
  and and_29 (S28, A28, not_1_out);
  and and_30 (S29, A29, not_1_out);
  and and_31 (S30, A30, not_1_out);
  and and_32 (S31, A31, not_1_out);
endmodule

module sum_sb (
  input  A31,
  input  A30,
  input  A29,
  input  A28,
  input  A27,
  input  A26,
  input  A25,
  input  A24,
  input  A23,
  input  A22,
  input  A21,
  input  A20,
  input  A19,
  input  A18,
  input  A17,
  input  A16,
  input  A15,
  input  A14,
  input  A13,
  input  A12,
  input  A11,
  input  A10,
  input  A9,
  input  A8,
  input  A7,
  input  A6,
  input  A5,
  input  A4,
  input  A3,
  input  A2,
  input  A1,
  input  A0,
  input  Sb,
  output S0,
  output S1,
  output S2,
  output S3,
  output S4,
  output S5,
  output S6,
  output S7,
  output S8,
  output S9,
  output S10,
  output S11,
  output S12,
  output S13,
  output S14,
  output S15,
  output S16,
  output S17,
  output S18,
  output S19,
  output S20,
  output S21,
  output S22,
  output S23,
  output S24,
  output S25,
  output S26,
  output S27,
  output S28,
  output S29,
  output S30,
  output S31
);

  or or_1 (S0, A0, Sb);
  or or_2 (S1, A1, Sb);
  or or_3 (S2, A2, Sb);
  or or_4 (S3, A3, Sb);
  or or_5 (S4, A4, Sb);
  or or_6 (S5, A5, Sb);
  or or_7 (S6, A6, Sb);
  or or_8 (S7, A7, Sb);
  or or_9 (S8, A8, Sb);
  or or_10 (S9, A9, Sb);
  or or_11 (S10, A10, Sb);
  or or_12 (S11, A11, Sb);
  or or_13 (S12, A12, Sb);
  or or_14 (S13, A13, Sb);
  or or_15 (S14, A14, Sb);
  or or_16 (S15, A15, Sb);
  or or_17 (S16, A16, Sb);
  or or_18 (S17, A17, Sb);
  or or_19 (S18, A18, Sb);
  or or_20 (S19, A19, Sb);
  or or_21 (S20, A20, Sb);
  or or_22 (S21, A21, Sb);
  or or_23 (S22, A22, Sb);
  or or_24 (S23, A23, Sb);
  or or_25 (S24, A24, Sb);
  or or_26 (S25, A25, Sb);
  or or_27 (S26, A26, Sb);
  or or_28 (S27, A27, Sb);
  or or_29 (S28, A28, Sb);
  or or_30 (S29, A29, Sb);
  or or_31 (S30, A30, Sb);
  or or_32 (S31, A31, Sb);
endmodule

module inverter_32bits (
  input  A31,
  input  A30,
  input  A29,
  input  A28,
  input  A27,
  input  A26,
  input  A25,
  input  A24,
  input  A23,
  input  A22,
  input  A21,
  input  A20,
  input  A19,
  input  A18,
  input  A17,
  input  A16,
  input  A15,
  input  A14,
  input  A13,
  input  A12,
  input  A11,
  input  A10,
  input  A9,
  input  A8,
  input  A7,
  input  A6,
  input  A5,
  input  A4,
  input  A3,
  input  A2,
  input  A1,
  input  A0,
  input  M,
  output S0,
  output S1,
  output S2,
  output S3,
  output S4,
  output S5,
  output S6,
  output S7,
  output S8,
  output S9,
  output S10,
  output S11,
  output S12,
  output S13,
  output S14,
  output S15,
  output S16,
  output S17,
  output S18,
  output S19,
  output S20,
  output S21,
  output S22,
  output S23,
  output S24,
  output S25,
  output S26,
  output S27,
  output S28,
  output S29,
  output S30,
  output S31
);

  xor xor_1 (S0, A0, M);
  xor xor_2 (S1, A1, M);
  xor xor_3 (S2, A2, M);
  xor xor_4 (S3, A3, M);
  xor xor_5 (S4, A4, M);
  xor xor_6 (S5, A5, M);
  xor xor_7 (S6, A6, M);
  xor xor_8 (S7, A7, M);
  xor xor_9 (S8, A8, M);
  xor xor_10 (S9, A9, M);
  xor xor_11 (S10, A10, M);
  xor xor_12 (S11, A11, M);
  xor xor_13 (S12, A12, M);
  xor xor_14 (S13, A13, M);
  xor xor_15 (S14, A14, M);
  xor xor_16 (S15, A15, M);
  xor xor_17 (S16, A16, M);
  xor xor_18 (S17, A17, M);
  xor xor_19 (S18, A18, M);
  xor xor_20 (S19, A19, M);
  xor xor_21 (S20, A20, M);
  xor xor_22 (S21, A21, M);
  xor xor_23 (S22, A22, M);
  xor xor_24 (S23, A23, M);
  xor xor_25 (S24, A24, M);
  xor xor_26 (S25, A25, M);
  xor xor_27 (S26, A26, M);
  xor xor_28 (S27, A27, M);
  xor xor_29 (S28, A28, M);
  xor xor_30 (S29, A29, M);
  xor xor_31 (S30, A30, M);
  xor xor_32 (S31, A31, M);
endmodule

module ALU (
  input  Oper_1,
  input  Oper_0,
  output S0,
  output S1,
  output S2,
  output S3,
  output S4,
  output S5,
  output S6,
  output S7,
  output S8,
  output S9,
  output S10,
  output S11,
  output S12,
  output S13,
  output S14,
  output S15,
  output S16,
  output S17,
  output S18,
  output S19,
  output S20,
  output S21,
  output S22,
  output S23,
  output S24,
  output S25,
  output S26,
  output S27,
  output S28,
  output S29,
  output S30,
  output S31
);

  wire and_32bits_1_s0, and_32bits_1_s1, and_32bits_1_s2, and_32bits_1_s3, and_32bits_1_s4, and_32bits_1_s5,
       and_32bits_1_s6, and_32bits_1_s7, and_32bits_1_s8, and_32bits_1_s9, and_32bits_1_s10,
       and_32bits_1_s11, and_32bits_1_s12, and_32bits_1_s13, and_32bits_1_s14, and_32bits_1_s15,
       and_32bits_1_s16, and_32bits_1_s17, and_32bits_1_s18, and_32bits_1_s19, and_32bits_1_s20,
       and_32bits_1_s21, and_32bits_1_s22, and_32bits_1_s23, and_32bits_1_s24, and_32bits_1_s25,
       and_32bits_1_s26, and_32bits_1_s27, and_32bits_1_s28, and_32bits_1_s29, and_32bits_1_s30,
       and_32bits_1_s31, not_1_out, not_2_out, or_32bits_1_s0, or_32bits_1_s1, or_32bits_1_s2,
       or_32bits_1_s3, or_32bits_1_s4, or_32bits_1_s5, or_32bits_1_s6, or_32bits_1_s7, or_32bits_1_s8,
       or_32bits_1_s9, or_32bits_1_s10, or_32bits_1_s11, or_32bits_1_s12, or_32bits_1_s13, or_32bits_1_s14,
       or_32bits_1_s15, or_32bits_1_s16, or_32bits_1_s17, or_32bits_1_s18, or_32bits_1_s19, or_32bits_1_s20,
       or_32bits_1_s21, or_32bits_1_s22, or_32bits_1_s23, or_32bits_1_s24, or_32bits_1_s25, or_32bits_1_s26,
       or_32bits_1_s27, or_32bits_1_s28, or_32bits_1_s29, or_32bits_1_s30, or_32bits_1_s31, or_32bits_2_s0,
       or_32bits_2_s1, or_32bits_2_s2, or_32bits_2_s3, or_32bits_2_s4, or_32bits_2_s5, or_32bits_2_s6,
       or_32bits_2_s7, or_32bits_2_s8, or_32bits_2_s9, or_32bits_2_s10, or_32bits_2_s11, or_32bits_2_s12,
       or_32bits_2_s13, or_32bits_2_s14, or_32bits_2_s15, or_32bits_2_s16, or_32bits_2_s17, or_32bits_2_s18,
       or_32bits_2_s19, or_32bits_2_s20, or_32bits_2_s21, or_32bits_2_s22, or_32bits_2_s23, or_32bits_2_s24,
       or_32bits_2_s25, or_32bits_2_s26, or_32bits_2_s27, or_32bits_2_s28, or_32bits_2_s29, or_32bits_2_s30,
       or_32bits_2_s31, or_32bits_3_s0, or_32bits_3_s1, or_32bits_3_s2, or_32bits_3_s3, or_32bits_3_s4,
       or_32bits_3_s5, or_32bits_3_s6, or_32bits_3_s7, or_32bits_3_s8, or_32bits_3_s9, or_32bits_3_s10,
       or_32bits_3_s11, or_32bits_3_s12, or_32bits_3_s13, or_32bits_3_s14, or_32bits_3_s15, or_32bits_3_s16,
       or_32bits_3_s17, or_32bits_3_s18, or_32bits_3_s19, or_32bits_3_s20, or_32bits_3_s21, or_32bits_3_s22,
       or_32bits_3_s23, or_32bits_3_s24, or_32bits_3_s25, or_32bits_3_s26, or_32bits_3_s27, or_32bits_3_s28,
       or_32bits_3_s29, or_32bits_3_s30, or_32bits_3_s31, somador_32bits_1_s0, somador_32bits_1_s1,
       somador_32bits_1_s2, somador_32bits_1_s3, somador_32bits_1_s4, somador_32bits_1_s5,
       somador_32bits_1_s6, somador_32bits_1_s7, somador_32bits_1_s8, somador_32bits_1_s9,
       somador_32bits_1_s10, somador_32bits_1_s11, somador_32bits_1_s12, somador_32bits_1_s13,
       somador_32bits_1_s14, somador_32bits_1_s15, somador_32bits_1_s16, somador_32bits_1_s17,
       somador_32bits_1_s18, somador_32bits_1_s19, somador_32bits_1_s20, somador_32bits_1_s21,
       somador_32bits_1_s22, somador_32bits_1_s23, somador_32bits_1_s24, somador_32bits_1_s25,
       somador_32bits_1_s26, somador_32bits_1_s27, somador_32bits_1_s28, somador_32bits_1_s29,
       somador_32bits_1_s30, somador_32bits_1_s31, sum_sa_1_s0, sum_sa_1_s1, sum_sa_1_s2, sum_sa_1_s3,
       sum_sa_1_s4, sum_sa_1_s5, sum_sa_1_s6, sum_sa_1_s7, sum_sa_1_s8, sum_sa_1_s9, sum_sa_1_s10,
       sum_sa_1_s11, sum_sa_1_s12, sum_sa_1_s13, sum_sa_1_s14, sum_sa_1_s15, sum_sa_1_s16, sum_sa_1_s17,
       sum_sa_1_s18, sum_sa_1_s19, sum_sa_1_s20, sum_sa_1_s21, sum_sa_1_s22, sum_sa_1_s23, sum_sa_1_s24,
       sum_sa_1_s25, sum_sa_1_s26, sum_sa_1_s27, sum_sa_1_s28, sum_sa_1_s29, sum_sa_1_s30, sum_sa_1_s31,
       sum_sa_2_s0, sum_sa_2_s1, sum_sa_2_s2, sum_sa_2_s3, sum_sa_2_s4, sum_sa_2_s5, sum_sa_2_s6,
       sum_sa_2_s7, sum_sa_2_s8, sum_sa_2_s9, sum_sa_2_s10, sum_sa_2_s11, sum_sa_2_s12, sum_sa_2_s13,
       sum_sa_2_s14, sum_sa_2_s15, sum_sa_2_s16, sum_sa_2_s17, sum_sa_2_s18, sum_sa_2_s19, sum_sa_2_s20,
       sum_sa_2_s21, sum_sa_2_s22, sum_sa_2_s23, sum_sa_2_s24, sum_sa_2_s25, sum_sa_2_s26, sum_sa_2_s27,
       sum_sa_2_s28, sum_sa_2_s29, sum_sa_2_s30, sum_sa_2_s31, sum_sa_3_s0, sum_sa_3_s1, sum_sa_3_s2,
       sum_sa_3_s3, sum_sa_3_s4, sum_sa_3_s5, sum_sa_3_s6, sum_sa_3_s7, sum_sa_3_s8, sum_sa_3_s9,
       sum_sa_3_s10, sum_sa_3_s11, sum_sa_3_s12, sum_sa_3_s13, sum_sa_3_s14, sum_sa_3_s15, sum_sa_3_s16,
       sum_sa_3_s17, sum_sa_3_s18, sum_sa_3_s19, sum_sa_3_s20, sum_sa_3_s21, sum_sa_3_s22, sum_sa_3_s23,
       sum_sa_3_s24, sum_sa_3_s25, sum_sa_3_s26, sum_sa_3_s27, sum_sa_3_s28, sum_sa_3_s29, sum_sa_3_s30,
       sum_sa_3_s31, sum_sa_4_s0, sum_sa_4_s1, sum_sa_4_s2, sum_sa_4_s3, sum_sa_4_s4, sum_sa_4_s5,
       sum_sa_4_s6, sum_sa_4_s7, sum_sa_4_s8, sum_sa_4_s9, sum_sa_4_s10, sum_sa_4_s11, sum_sa_4_s12,
       sum_sa_4_s13, sum_sa_4_s14, sum_sa_4_s15, sum_sa_4_s16, sum_sa_4_s17, sum_sa_4_s18, sum_sa_4_s19,
       sum_sa_4_s20, sum_sa_4_s21, sum_sa_4_s22, sum_sa_4_s23, sum_sa_4_s24, sum_sa_4_s25, sum_sa_4_s26,
       sum_sa_4_s27, sum_sa_4_s28, sum_sa_4_s29, sum_sa_4_s30, sum_sa_4_s31, undriven, undriven_2,
       undriven_3, undriven_4, undriven_5, undriven_6, undriven_7, undriven_8, undriven_9, undriven_10,
       undriven_11, undriven_12, undriven_13, undriven_14, undriven_15, undriven_16, undriven_17,
       undriven_18, undriven_19, undriven_20, undriven_21, undriven_22, undriven_23, undriven_24,
       undriven_25, undriven_26, undriven_27, undriven_28, undriven_29, undriven_30, undriven_31,
       undriven_32, xor_32bits_1_s0, xor_32bits_1_s1, xor_32bits_1_s2, xor_32bits_1_s3, xor_32bits_1_s4,
       xor_32bits_1_s5, xor_32bits_1_s6, xor_32bits_1_s7, xor_32bits_1_s8, xor_32bits_1_s9, xor_32bits_1_s10,
       xor_32bits_1_s11, xor_32bits_1_s12, xor_32bits_1_s13, xor_32bits_1_s14, xor_32bits_1_s15,
       xor_32bits_1_s16, xor_32bits_1_s17, xor_32bits_1_s18, xor_32bits_1_s19, xor_32bits_1_s20,
       xor_32bits_1_s21, xor_32bits_1_s22, xor_32bits_1_s23, xor_32bits_1_s24, xor_32bits_1_s25,
       xor_32bits_1_s26, xor_32bits_1_s27, xor_32bits_1_s28, xor_32bits_1_s29, xor_32bits_1_s30;

  AND_32Bits and_32bits_1 (
    .A31(undriven), .A30(undriven_2), .A29(undriven_3), .A28(undriven_4), .A27(undriven_5), .A26(undriven_6),
    .A25(undriven_7), .A24(undriven_8), .A23(undriven_9), .A22(undriven_10), .A21(undriven_11),
    .A20(undriven_12), .A19(undriven_13), .A18(undriven_14), .A17(undriven_15), .A16(undriven_16),
    .A15(undriven_17), .A14(undriven_18), .A13(undriven_19), .A12(undriven_20), .A11(undriven_21),
    .A10(undriven_22), .A9(undriven_23), .A8(undriven_24), .A7(undriven_25), .A6(undriven_26),
    .A5(undriven_27), .A4(undriven_28), .A3(undriven_29), .A2(undriven_30), .A1(undriven_31),
    .A0(undriven_32), .S0(and_32bits_1_s0), .S1(and_32bits_1_s1), .S2(and_32bits_1_s2), .S3(and_32bits_1_s3),
    .S4(and_32bits_1_s4), .S5(and_32bits_1_s5), .S6(and_32bits_1_s6), .S7(and_32bits_1_s7),
    .S8(and_32bits_1_s8), .S9(and_32bits_1_s9), .S10(and_32bits_1_s10), .S11(and_32bits_1_s11),
    .S12(and_32bits_1_s12), .S13(and_32bits_1_s13), .S14(and_32bits_1_s14), .S15(and_32bits_1_s15),
    .S16(and_32bits_1_s16), .S17(and_32bits_1_s17), .S18(and_32bits_1_s18), .S19(and_32bits_1_s19),
    .S20(and_32bits_1_s20), .S21(and_32bits_1_s21), .S22(and_32bits_1_s22), .S23(and_32bits_1_s23),
    .S24(and_32bits_1_s24), .S25(and_32bits_1_s25), .S26(and_32bits_1_s26), .S27(and_32bits_1_s27),
    .S28(and_32bits_1_s28), .S29(and_32bits_1_s29), .S30(and_32bits_1_s30), .S31(and_32bits_1_s31));  // open: B31, B30, B29, B28, B27, B26, B25, B24, B23, B22, B21, B20, B19, B18, B17, B16, B15, B14, B13, B12, B11, B10, B9, B8, B7, B6, B5, B4, B3, B2, B1, B0
  OR_32Bits or_32bits_1 (
    .S0(or_32bits_1_s0), .S1(or_32bits_1_s1), .S2(or_32bits_1_s2), .S3(or_32bits_1_s3), .S4(or_32bits_1_s4),
    .S5(or_32bits_1_s5), .S6(or_32bits_1_s6), .S7(or_32bits_1_s7), .S8(or_32bits_1_s8), .S9(or_32bits_1_s9),
    .S10(or_32bits_1_s10), .S11(or_32bits_1_s11), .S12(or_32bits_1_s12), .S13(or_32bits_1_s13),
    .S14(or_32bits_1_s14), .S15(or_32bits_1_s15), .S16(or_32bits_1_s16), .S17(or_32bits_1_s17),
    .S18(or_32bits_1_s18), .S19(or_32bits_1_s19), .S20(or_32bits_1_s20), .S21(or_32bits_1_s21),
    .S22(or_32bits_1_s22), .S23(or_32bits_1_s23), .S24(or_32bits_1_s24), .S25(or_32bits_1_s25),
    .S26(or_32bits_1_s26), .S27(or_32bits_1_s27), .S28(or_32bits_1_s28), .S29(or_32bits_1_s29),
    .S30(or_32bits_1_s30), .S31(or_32bits_1_s31));  // open: A31, A30, A29, A28, A27, A26, A25, A24, A23, A22, A21, A20, A19, A18, A17, A16, A15, A14, A13, A12, A11, A10, A9, A8, A7, A6, A5, A4, A3, A2, A1, A0, B31, B30, B29, B28, B27, B26, B25, B24, B23, B22, B21, B20, B19, B18, B17, B16, B15, B14, B13, B12, B11, B10, B9, B8, B7, B6, B5, B4, B3, B2, B1, B0
  XOR_32bits xor_32bits_1 (
    .S0(xor_32bits_1_s0), .S1(xor_32bits_1_s1), .S2(xor_32bits_1_s2), .S3(xor_32bits_1_s3),
    .S4(xor_32bits_1_s4), .S5(xor_32bits_1_s5), .S6(xor_32bits_1_s6), .S7(xor_32bits_1_s7),
    .S8(xor_32bits_1_s8), .S9(xor_32bits_1_s9), .S10(xor_32bits_1_s10), .S11(xor_32bits_1_s11),
    .S12(xor_32bits_1_s12), .S13(xor_32bits_1_s13), .S14(xor_32bits_1_s14), .S15(xor_32bits_1_s15),
    .S16(xor_32bits_1_s16), .S17(xor_32bits_1_s17), .S18(xor_32bits_1_s18), .S19(xor_32bits_1_s19),
    .S20(xor_32bits_1_s20), .S21(xor_32bits_1_s21), .S22(xor_32bits_1_s22), .S23(xor_32bits_1_s23),
    .S24(xor_32bits_1_s24), .S25(xor_32bits_1_s25), .S26(xor_32bits_1_s26), .S27(xor_32bits_1_s27),
    .S28(xor_32bits_1_s28), .S29(xor_32bits_1_s29), .S30(xor_32bits_1_s30));  // open: A31, A30, A29, A28, A27, A26, A25, A24, A23, A22, A21, A20, A19, A18, A17, A16, A15, A14, A13, A12, A11, A10, A9, A8, A7, A6, A5, A4, A3, A2, A1, A0, B31, B30, B29, B28, B27, B26, B25, B24, B23, B22, B21, B20, B19, B18, B17, B16, B15, B14, B13, B12, B11, B10, B9, B8, B7, B6, B5, B4, B3, B2, B1, B0, S31
  SOMADOR_32bits somador_32bits_1 (
    .S0(somador_32bits_1_s0), .S1(somador_32bits_1_s1), .S2(somador_32bits_1_s2), .S3(somador_32bits_1_s3),
    .S4(somador_32bits_1_s4), .S5(somador_32bits_1_s5), .S6(somador_32bits_1_s6), .S7(somador_32bits_1_s7),
    .S8(somador_32bits_1_s8), .S9(somador_32bits_1_s9), .S10(somador_32bits_1_s10),
    .S11(somador_32bits_1_s11), .S12(somador_32bits_1_s12), .S13(somador_32bits_1_s13),
    .S14(somador_32bits_1_s14), .S15(somador_32bits_1_s15), .S16(somador_32bits_1_s16),
    .S17(somador_32bits_1_s17), .S18(somador_32bits_1_s18), .S19(somador_32bits_1_s19),
    .S20(somador_32bits_1_s20), .S21(somador_32bits_1_s21), .S22(somador_32bits_1_s22),
    .S23(somador_32bits_1_s23), .S24(somador_32bits_1_s24), .S25(somador_32bits_1_s25),
    .S26(somador_32bits_1_s26), .S27(somador_32bits_1_s27), .S28(somador_32bits_1_s28),
    .S29(somador_32bits_1_s29), .S30(somador_32bits_1_s30), .S31(somador_32bits_1_s31));  // open: A31, A30, A29, A28, A27, A26, A25, A24, A23, A22, A21, A20, A19, A18, A17, A16, A15, A14, A13, A12, A11, A10, A9, A8, A7, A6, A5, A4, A3, A2, A1, A0, M, B31, B30, B29, B28, B27, B26, B25, B24, B23, B22, B21, B20, B19, B18, B17, B16, B15, B14, B13, B12, B11, B10, B9, B8, B7, B6, B5, B4, B3, B2, B1, B0, Cout, OVFL
  not not_1 (not_1_out, Oper_1);
  not not_2 (not_2_out, Oper_0);
  sum_sa sum_sa_1 (
    .A31(or_32bits_1_s0), .A30(or_32bits_1_s1), .A29(or_32bits_1_s2), .A28(or_32bits_1_s3),
    .A27(or_32bits_1_s4), .A26(or_32bits_1_s5), .A25(or_32bits_1_s6), .A24(or_32bits_1_s7),
    .A23(or_32bits_1_s8), .A22(or_32bits_1_s9), .A21(or_32bits_1_s10), .A20(or_32bits_1_s11),
    .A19(or_32bits_1_s12), .A18(or_32bits_1_s13), .A17(or_32bits_1_s14), .A16(or_32bits_1_s15),
    .A15(or_32bits_1_s16), .A14(or_32bits_1_s17), .A13(or_32bits_1_s18), .A12(or_32bits_1_s19),
    .A11(or_32bits_1_s20), .A10(or_32bits_1_s21), .A9(or_32bits_1_s22), .A8(or_32bits_1_s23),
    .A7(or_32bits_1_s24), .A6(or_32bits_1_s25), .A5(or_32bits_1_s26), .A4(or_32bits_1_s27),
    .A3(or_32bits_1_s28), .A2(or_32bits_1_s29), .A1(or_32bits_1_s30), .A0(or_32bits_1_s31), .Sa(Oper_1),
    .S0(sum_sa_1_s0), .S1(sum_sa_1_s1), .S2(sum_sa_1_s2), .S3(sum_sa_1_s3), .S4(sum_sa_1_s4),
    .S5(sum_sa_1_s5), .S6(sum_sa_1_s6), .S7(sum_sa_1_s7), .S8(sum_sa_1_s8), .S9(sum_sa_1_s9),
    .S10(sum_sa_1_s10), .S11(sum_sa_1_s11), .S12(sum_sa_1_s12), .S13(sum_sa_1_s13), .S14(sum_sa_1_s14),
    .S15(sum_sa_1_s15), .S16(sum_sa_1_s16), .S17(sum_sa_1_s17), .S18(sum_sa_1_s18), .S19(sum_sa_1_s19),
    .S20(sum_sa_1_s20), .S21(sum_sa_1_s21), .S22(sum_sa_1_s22), .S23(sum_sa_1_s23), .S24(sum_sa_1_s24),
    .S25(sum_sa_1_s25), .S26(sum_sa_1_s26), .S27(sum_sa_1_s27), .S28(sum_sa_1_s28), .S29(sum_sa_1_s29),
    .S30(sum_sa_1_s30), .S31(sum_sa_1_s31));
  sum_sa sum_sa_2 (
    .A31(somador_32bits_1_s0), .A30(somador_32bits_1_s1), .A29(somador_32bits_1_s2),
    .A28(somador_32bits_1_s3), .A27(somador_32bits_1_s4), .A26(somador_32bits_1_s5),
    .A25(somador_32bits_1_s6), .A24(somador_32bits_1_s7), .A23(somador_32bits_1_s8),
    .A22(somador_32bits_1_s9), .A21(somador_32bits_1_s10), .A20(somador_32bits_1_s11),
    .A19(somador_32bits_1_s12), .A18(somador_32bits_1_s13), .A17(somador_32bits_1_s14),
    .A16(somador_32bits_1_s15), .A15(somador_32bits_1_s16), .A14(somador_32bits_1_s17),
    .A13(somador_32bits_1_s18), .A12(somador_32bits_1_s19), .A11(somador_32bits_1_s20),
    .A10(somador_32bits_1_s21), .A9(somador_32bits_1_s22), .A8(somador_32bits_1_s23),
    .A7(somador_32bits_1_s24), .A6(somador_32bits_1_s25), .A5(somador_32bits_1_s26),
    .A4(somador_32bits_1_s27), .A3(somador_32bits_1_s28), .A2(somador_32bits_1_s29),
    .A1(somador_32bits_1_s30), .A0(somador_32bits_1_s31), .Sa(Oper_0), .S0(sum_sa_2_s0), .S1(sum_sa_2_s1),
    .S2(sum_sa_2_s2), .S3(sum_sa_2_s3), .S4(sum_sa_2_s4), .S5(sum_sa_2_s5), .S6(sum_sa_2_s6),
    .S7(sum_sa_2_s7), .S8(sum_sa_2_s8), .S9(sum_sa_2_s9), .S10(sum_sa_2_s10), .S11(sum_sa_2_s11),
    .S12(sum_sa_2_s12), .S13(sum_sa_2_s13), .S14(sum_sa_2_s14), .S15(sum_sa_2_s15), .S16(sum_sa_2_s16),
    .S17(sum_sa_2_s17), .S18(sum_sa_2_s18), .S19(sum_sa_2_s19), .S20(sum_sa_2_s20), .S21(sum_sa_2_s21),
    .S22(sum_sa_2_s22), .S23(sum_sa_2_s23), .S24(sum_sa_2_s24), .S25(sum_sa_2_s25), .S26(sum_sa_2_s26),
    .S27(sum_sa_2_s27), .S28(sum_sa_2_s28), .S29(sum_sa_2_s29), .S30(sum_sa_2_s30), .S31(sum_sa_2_s31));
  sum_sa sum_sa_3 (
    .A31(and_32bits_1_s0), .A30(and_32bits_1_s1), .A29(and_32bits_1_s2), .A28(and_32bits_1_s3),
    .A27(and_32bits_1_s4), .A26(and_32bits_1_s5), .A25(and_32bits_1_s6), .A24(and_32bits_1_s7),
    .A23(and_32bits_1_s8), .A22(and_32bits_1_s9), .A21(and_32bits_1_s10), .A20(and_32bits_1_s11),
    .A19(and_32bits_1_s12), .A18(and_32bits_1_s13), .A17(and_32bits_1_s14), .A16(and_32bits_1_s15),
    .A15(and_32bits_1_s16), .A14(and_32bits_1_s17), .A13(and_32bits_1_s18), .A12(and_32bits_1_s19),
    .A11(and_32bits_1_s20), .A10(and_32bits_1_s21), .A9(and_32bits_1_s22), .A8(and_32bits_1_s23),
    .A7(and_32bits_1_s24), .A6(and_32bits_1_s25), .A5(and_32bits_1_s26), .A4(and_32bits_1_s27),
    .A3(and_32bits_1_s28), .A2(and_32bits_1_s29), .A1(and_32bits_1_s30), .A0(and_32bits_1_s31),
    .Sa(not_1_out), .S0(sum_sa_3_s0), .S1(sum_sa_3_s1), .S2(sum_sa_3_s2), .S3(sum_sa_3_s3), .S4(sum_sa_3_s4),
    .S5(sum_sa_3_s5), .S6(sum_sa_3_s6), .S7(sum_sa_3_s7), .S8(sum_sa_3_s8), .S9(sum_sa_3_s9),
    .S10(sum_sa_3_s10), .S11(sum_sa_3_s11), .S12(sum_sa_3_s12), .S13(sum_sa_3_s13), .S14(sum_sa_3_s14),
    .S15(sum_sa_3_s15), .S16(sum_sa_3_s16), .S17(sum_sa_3_s17), .S18(sum_sa_3_s18), .S19(sum_sa_3_s19),
    .S20(sum_sa_3_s20), .S21(sum_sa_3_s21), .S22(sum_sa_3_s22), .S23(sum_sa_3_s23), .S24(sum_sa_3_s24),
    .S25(sum_sa_3_s25), .S26(sum_sa_3_s26), .S27(sum_sa_3_s27), .S28(sum_sa_3_s28), .S29(sum_sa_3_s29),
    .S30(sum_sa_3_s30), .S31(sum_sa_3_s31));
  OR_32Bits or_32bits_2 (
    .A31(sum_sa_3_s0), .A30(sum_sa_3_s1), .A29(sum_sa_3_s2), .A28(sum_sa_3_s3), .A27(sum_sa_3_s4),
    .A26(sum_sa_3_s5), .A25(sum_sa_3_s6), .A24(sum_sa_3_s7), .A23(sum_sa_3_s8), .A22(sum_sa_3_s9),
    .A21(sum_sa_3_s10), .A20(sum_sa_3_s11), .A19(sum_sa_3_s12), .A18(sum_sa_3_s13), .A17(sum_sa_3_s14),
    .A16(sum_sa_3_s15), .A15(sum_sa_3_s16), .A14(sum_sa_3_s17), .A13(sum_sa_3_s18), .A12(sum_sa_3_s19),
    .A11(sum_sa_3_s20), .A10(sum_sa_3_s21), .A9(sum_sa_3_s22), .A8(sum_sa_3_s23), .A7(sum_sa_3_s24),
    .A6(sum_sa_3_s25), .A5(sum_sa_3_s26), .A4(sum_sa_3_s27), .A3(sum_sa_3_s28), .A2(sum_sa_3_s29),
    .A1(sum_sa_3_s30), .A0(sum_sa_3_s31), .B31(sum_sa_1_s0), .B30(sum_sa_1_s1), .B29(sum_sa_1_s2),
    .B28(sum_sa_1_s3), .B27(sum_sa_1_s4), .B26(sum_sa_1_s5), .B25(sum_sa_1_s6), .B24(sum_sa_1_s7),
    .B23(sum_sa_1_s8), .B22(sum_sa_1_s9), .B21(sum_sa_1_s10), .B20(sum_sa_1_s11), .B19(sum_sa_1_s12),
    .B18(sum_sa_1_s13), .B17(sum_sa_1_s14), .B16(sum_sa_1_s15), .B15(sum_sa_1_s16), .B14(sum_sa_1_s17),
    .B13(sum_sa_1_s18), .B12(sum_sa_1_s19), .B11(sum_sa_1_s20), .B10(sum_sa_1_s21), .B9(sum_sa_1_s22),
    .B8(sum_sa_1_s23), .B7(sum_sa_1_s24), .B6(sum_sa_1_s25), .B5(sum_sa_1_s26), .B4(sum_sa_1_s27),
    .B3(sum_sa_1_s28), .B2(sum_sa_1_s29), .B1(sum_sa_1_s30), .B0(sum_sa_1_s31), .S0(or_32bits_2_s0),
    .S1(or_32bits_2_s1), .S2(or_32bits_2_s2), .S3(or_32bits_2_s3), .S4(or_32bits_2_s4), .S5(or_32bits_2_s5),
    .S6(or_32bits_2_s6), .S7(or_32bits_2_s7), .S8(or_32bits_2_s8), .S9(or_32bits_2_s9),
    .S10(or_32bits_2_s10), .S11(or_32bits_2_s11), .S12(or_32bits_2_s12), .S13(or_32bits_2_s13),
    .S14(or_32bits_2_s14), .S15(or_32bits_2_s15), .S16(or_32bits_2_s16), .S17(or_32bits_2_s17),
    .S18(or_32bits_2_s18), .S19(or_32bits_2_s19), .S20(or_32bits_2_s20), .S21(or_32bits_2_s21),
    .S22(or_32bits_2_s22), .S23(or_32bits_2_s23), .S24(or_32bits_2_s24), .S25(or_32bits_2_s25),
    .S26(or_32bits_2_s26), .S27(or_32bits_2_s27), .S28(or_32bits_2_s28), .S29(or_32bits_2_s29),
    .S30(or_32bits_2_s30), .S31(or_32bits_2_s31));
  sum_sa sum_sa_4 (
    .A31(xor_32bits_1_s0), .A30(xor_32bits_1_s1), .A29(xor_32bits_1_s2), .A28(xor_32bits_1_s3),
    .A27(xor_32bits_1_s4), .A26(xor_32bits_1_s5), .A25(xor_32bits_1_s6), .A24(xor_32bits_1_s7),
    .A23(xor_32bits_1_s8), .A22(xor_32bits_1_s9), .A21(xor_32bits_1_s10), .A20(xor_32bits_1_s11),
    .A19(xor_32bits_1_s12), .A18(xor_32bits_1_s13), .A17(xor_32bits_1_s14), .A16(xor_32bits_1_s15),
    .A15(xor_32bits_1_s16), .A14(xor_32bits_1_s17), .A13(xor_32bits_1_s18), .A12(xor_32bits_1_s19),
    .A11(xor_32bits_1_s20), .A10(xor_32bits_1_s21), .A9(xor_32bits_1_s22), .A8(xor_32bits_1_s23),
    .A7(xor_32bits_1_s24), .A6(xor_32bits_1_s25), .A5(xor_32bits_1_s26), .A4(xor_32bits_1_s27),
    .A3(xor_32bits_1_s28), .A2(xor_32bits_1_s29), .A1(xor_32bits_1_s30), .Sa(not_2_out), .S0(sum_sa_4_s0),
    .S1(sum_sa_4_s1), .S2(sum_sa_4_s2), .S3(sum_sa_4_s3), .S4(sum_sa_4_s4), .S5(sum_sa_4_s5),
    .S6(sum_sa_4_s6), .S7(sum_sa_4_s7), .S8(sum_sa_4_s8), .S9(sum_sa_4_s9), .S10(sum_sa_4_s10),
    .S11(sum_sa_4_s11), .S12(sum_sa_4_s12), .S13(sum_sa_4_s13), .S14(sum_sa_4_s14), .S15(sum_sa_4_s15),
    .S16(sum_sa_4_s16), .S17(sum_sa_4_s17), .S18(sum_sa_4_s18), .S19(sum_sa_4_s19), .S20(sum_sa_4_s20),
    .S21(sum_sa_4_s21), .S22(sum_sa_4_s22), .S23(sum_sa_4_s23), .S24(sum_sa_4_s24), .S25(sum_sa_4_s25),
    .S26(sum_sa_4_s26), .S27(sum_sa_4_s27), .S28(sum_sa_4_s28), .S29(sum_sa_4_s29), .S30(sum_sa_4_s30),
    .S31(sum_sa_4_s31));  // open: A0
  OR_32Bits or_32bits_3 (
    .A31(sum_sa_4_s0), .A30(sum_sa_4_s1), .A29(sum_sa_4_s2), .A28(sum_sa_4_s3), .A27(sum_sa_4_s4),
    .A26(sum_sa_4_s5), .A25(sum_sa_4_s6), .A24(sum_sa_4_s7), .A23(sum_sa_4_s8), .A22(sum_sa_4_s9),
    .A21(sum_sa_4_s10), .A20(sum_sa_4_s11), .A19(sum_sa_4_s12), .A18(sum_sa_4_s13), .A17(sum_sa_4_s14),
    .A16(sum_sa_4_s15), .A15(sum_sa_4_s16), .A14(sum_sa_4_s17), .A13(sum_sa_4_s18), .A12(sum_sa_4_s19),
    .A11(sum_sa_4_s20), .A10(sum_sa_4_s21), .A9(sum_sa_4_s22), .A8(sum_sa_4_s23), .A7(sum_sa_4_s24),
    .A6(sum_sa_4_s25), .A5(sum_sa_4_s26), .A4(sum_sa_4_s27), .A3(sum_sa_4_s28), .A2(sum_sa_4_s29),
    .A1(sum_sa_4_s30), .A0(sum_sa_4_s31), .B31(sum_sa_2_s0), .B30(sum_sa_2_s1), .B29(sum_sa_2_s2),
    .B28(sum_sa_2_s3), .B27(sum_sa_2_s4), .B26(sum_sa_2_s5), .B25(sum_sa_2_s6), .B24(sum_sa_2_s7),
    .B23(sum_sa_2_s8), .B22(sum_sa_2_s9), .B21(sum_sa_2_s10), .B20(sum_sa_2_s11), .B19(sum_sa_2_s12),
    .B18(sum_sa_2_s13), .B17(sum_sa_2_s14), .B16(sum_sa_2_s15), .B15(sum_sa_2_s16), .B14(sum_sa_2_s17),
    .B13(sum_sa_2_s18), .B12(sum_sa_2_s19), .B11(sum_sa_2_s20), .B10(sum_sa_2_s21), .B9(sum_sa_2_s22),
    .B8(sum_sa_2_s23), .B7(sum_sa_2_s24), .B6(sum_sa_2_s25), .B5(sum_sa_2_s26), .B4(sum_sa_2_s27),
    .B3(sum_sa_2_s28), .B2(sum_sa_2_s29), .B1(sum_sa_2_s30), .B0(sum_sa_2_s31), .S0(or_32bits_3_s0),
    .S1(or_32bits_3_s1), .S2(or_32bits_3_s2), .S3(or_32bits_3_s3), .S4(or_32bits_3_s4), .S5(or_32bits_3_s5),
    .S6(or_32bits_3_s6), .S7(or_32bits_3_s7), .S8(or_32bits_3_s8), .S9(or_32bits_3_s9),
    .S10(or_32bits_3_s10), .S11(or_32bits_3_s11), .S12(or_32bits_3_s12), .S13(or_32bits_3_s13),
    .S14(or_32bits_3_s14), .S15(or_32bits_3_s15), .S16(or_32bits_3_s16), .S17(or_32bits_3_s17),
    .S18(or_32bits_3_s18), .S19(or_32bits_3_s19), .S20(or_32bits_3_s20), .S21(or_32bits_3_s21),
    .S22(or_32bits_3_s22), .S23(or_32bits_3_s23), .S24(or_32bits_3_s24), .S25(or_32bits_3_s25),
    .S26(or_32bits_3_s26), .S27(or_32bits_3_s27), .S28(or_32bits_3_s28), .S29(or_32bits_3_s29),
    .S30(or_32bits_3_s30), .S31(or_32bits_3_s31));
  OR_32Bits or_32bits_4 (
    .A31(or_32bits_2_s0), .A30(or_32bits_2_s1), .A29(or_32bits_2_s2), .A28(or_32bits_2_s3),
    .A27(or_32bits_2_s4), .A26(or_32bits_2_s5), .A25(or_32bits_2_s6), .A24(or_32bits_2_s7),
    .A23(or_32bits_2_s8), .A22(or_32bits_2_s9), .A21(or_32bits_2_s10), .A20(or_32bits_2_s11),
    .A19(or_32bits_2_s12), .A18(or_32bits_2_s13), .A17(or_32bits_2_s14), .A16(or_32bits_2_s15),
    .A15(or_32bits_2_s16), .A14(or_32bits_2_s17), .A13(or_32bits_2_s18), .A12(or_32bits_2_s19),
    .A11(or_32bits_2_s20), .A10(or_32bits_2_s21), .A9(or_32bits_2_s22), .A8(or_32bits_2_s23),
    .A7(or_32bits_2_s24), .A6(or_32bits_2_s25), .A5(or_32bits_2_s26), .A4(or_32bits_2_s27),
    .A3(or_32bits_2_s28), .A2(or_32bits_2_s29), .A1(or_32bits_2_s30), .A0(or_32bits_2_s31),
    .B31(or_32bits_3_s0), .B30(or_32bits_3_s1), .B29(or_32bits_3_s2), .B28(or_32bits_3_s3),
    .B27(or_32bits_3_s4), .B26(or_32bits_3_s5), .B25(or_32bits_3_s6), .B24(or_32bits_3_s7),
    .B23(or_32bits_3_s8), .B22(or_32bits_3_s9), .B21(or_32bits_3_s10), .B20(or_32bits_3_s11),
    .B19(or_32bits_3_s12), .B18(or_32bits_3_s13), .B17(or_32bits_3_s14), .B16(or_32bits_3_s15),
    .B15(or_32bits_3_s16), .B14(or_32bits_3_s17), .B13(or_32bits_3_s18), .B12(or_32bits_3_s19),
    .B11(or_32bits_3_s20), .B10(or_32bits_3_s21), .B9(or_32bits_3_s22), .B8(or_32bits_3_s23),
    .B7(or_32bits_3_s24), .B6(or_32bits_3_s25), .B5(or_32bits_3_s26), .B4(or_32bits_3_s27),
    .B3(or_32bits_3_s28), .B2(or_32bits_3_s29), .B1(or_32bits_3_s30), .B0(or_32bits_3_s31), .S0(S0), .S1(S1),
    .S2(S2), .S3(S3), .S4(S4), .S5(S5), .S6(S6), .S7(S7), .S8(S8), .S9(S9), .S10(S10), .S11(S11), .S12(S12),
    .S13(S13), .S14(S14), .S15(S15), .S16(S16), .S17(S17), .S18(S18), .S19(S19), .S20(S20), .S21(S21),
    .S22(S22), .S23(S23), .S24(S24), .S25(S25), .S26(S26), .S27(S27), .S28(S28), .S29(S29), .S30(S30),
    .S31(S31));
endmodule
