// Logisim project sd_combinacionais.circ as structural Verilog: 8 circuits, main circuit mux_1x2
module mux_1x2 (
  input  A,
  input  B,
  input  S,
  output R
);

  wire and_1_out, and_2_out, not_1_out;

  not not_1 (not_1_out, S);
  and and_1 (and_1_out, A, not_1_out);
  and and_2 (and_2_out, B, S);
  or or_1 (R, and_1_out, and_2_out);
endmodule

module full_adder (
  input  Cin,
  input  A,
  input  B,
  output S
);

  wire xor_1_out;

  xor xor_1 (xor_1_out, A, B);
  xor xor_2 (S, Cin, xor_1_out);
endmodule

module somador_subtrator (
  input  M,
  input  A3,
  input  A2,
  input  A1,
  input  A0,
  input  B3,
  input  B2,
  input  B1,
  input  B0,
  output S3,
  output S2,
  output S1,
  output S0,
  output OVFL,
  output Cout
);

  wire and_1_out, and_2_out, and_3_out, and_4_out, and_5_out, and_6_out, and_7_out, and_8_out, and_9_out,
       and_10_out, G0_out, G1_out, G2_out, G3_out, or_1_out, or_2_out, or_3_out, P0_out, P1_out, P2_out,
       P3_out, xor_1_out, xor_2_out, xor_3_out, xor_4_out;

  xor xor_1 (xor_1_out, M, B3);
  xor xor_2 (xor_2_out, M, B0);
  xor xor_3 (xor_3_out, M, B1);
  xor xor_4 (xor_4_out, M, B2);
  and G1 (G1_out, xor_3_out, A1);
  or P1 (P1_out, xor_3_out, A1);
  and G0 (G0_out, A0, xor_2_out);
  or P0 (P0_out, A0, xor_2_out);
  and G2 (G2_out, xor_4_out, A2);
  or P2 (P2_out, xor_4_out, A2);
  and G3 (G3_out, xor_1_out, A3);
  or P3 (P3_out, xor_1_out, A3);
  and and_1 (and_1_out, P0_out, M);
  and and_2 (and_2_out, G0_out, P1_out);
  and and_3 (and_3_out, P1_out, M, P0_out);
  or or_1 (or_1_out, and_1_out, G0_out);
  and and_4 (and_4_out, G1_out, P2_out);
  and and_5 (and_5_out, P2_out, P1_out, G0_out);
  and and_6 (and_6_out, P2_out, P1_out, P0_out, M);
  and and_7 (and_7_out, P3_out, G2_out);
  and and_8 (and_8_out, P3_out, P2_out, G1_out);
  and and_9 (and_9_out, P3_out, P2_out, P1_out, G0_out);
  and and_10 (and_10_out, P3_out, P2_out, P1_out, P0_out, M);
  or or_2 (or_2_out, G1_out, and_2_out, and_3_out);
  or or_3 (or_3_out, G2_out, and_4_out, and_5_out, and_6_out);
  or or_4 (Cout, G3_out, and_7_out, and_8_out, and_9_out, and_10_out);
  full_adder full_adder_1 (.Cin(M), .A(A0), .B(xor_2_out), .S(S0));
  full_adder full_adder_2 (.Cin(or_1_out), .A(A1), .B(xor_3_out), .S(S1));
  full_adder full_adder_3 (.Cin(or_2_out), .A(A2), .B(xor_4_out), .S(S2));
  full_adder full_adder_4 (.Cin(or_3_out), .A(A3), .B(xor_1_out), .S(S3));
  xor xor_5 (OVFL, or_3_out, Cout);
endmodule

module comparator_1bit (
  input  A,
  input  B,
  output G,
  output E,
  output L
);

  wire not_1_out, not_2_out, or_1_out;

  not not_1 (not_1_out, B);
  not not_2 (not_2_out, A);
  and and_1 (G, A, not_1_out);
  and and_2 (L, not_2_out, B);
  or or_1 (or_1_out, G, L);
  not not_3 (E, or_1_out);
endmodule

module comparator_2btis (
  input  A0,
  input  A1,
  input  B0,
  input  B1,
  output G,
  output E,
  output L
);

  wire and_1_out, comparator_1bit_1_e, comparator_1bit_1_g, comparator_1bit_2_e, comparator_1bit_2_g;

  comparator_1bit comparator_1bit_1 (.G(comparator_1bit_1_g), .E(comparator_1bit_1_e), .A(A0), .B(B0));  // open: L
  comparator_1bit comparator_1bit_2 (.G(comparator_1bit_2_g), .E(comparator_1bit_2_e), .A(A1), .B(B1));  // open: L
  and and_1 (and_1_out, comparator_1bit_1_g, comparator_1bit_2_e);
  or or_1 (G, and_1_out, comparator_1bit_2_g);
  and and_2 (E, comparator_1bit_1_e, comparator_1bit_2_e);
  xnor xnor_1 (L, E, G);
endmodule

module comparator_4bits (
  input  A3,
  input  A2,
  input  A1,
  input  A0,
  input  B3,
  input  B2,
  input  B1,
  input  B0,
  output G,
  output E,
  output L
);

  wire and_1_out, comparator_2btis_1_e, comparator_2btis_1_g, comparator_2btis_2_e, comparator_2btis_2_g;

  comparator_2btis comparator_2btis_1 (
    .A0(A0), .A1(A1), .B0(B0), .B1(B1), .G(comparator_2btis_1_g), .E(comparator_2btis_1_e));  // open: L
  comparator_2btis comparator_2btis_2 (
    .A0(A2), .A1(A3), .B0(B2), .B1(B3), .G(comparator_2btis_2_g), .E(comparator_2btis_2_e));  // open: L
  and and_1 (and_1_out, comparator_2btis_1_g, comparator_2btis_2_e);
  or or_1 (G, and_1_out, comparator_2btis_2_g);
  and and_2 (E, comparator_2btis_1_e, comparator_2btis_2_e);
  xnor xnor_1 (L, E, G);
endmodule

module Tester (
  input  A3,
  input  A2,
  input  A1,
  input  A0,
  input  B3,
  input  B2,
  input  B1,
  input  B0,
  output G,
  output E,
  output L
);

  comparator_4bits comparator_4bits_1 (
    .A3(A3), .A2(A2), .A1(A1), .A0(A0), .B3(B3), .B2(B2), .B1(B1), .B0(B0), .G(G), .E(E), .L(L));
endmodule

module mux_2x4 (
  input  A0,
  input  A1,
  input  A2,
  input  A3,
  input  S1,
  input  S0,
  output X
);

  wire and_1_out, and_2_out, mux_1x2_1_r, mux_1x2_2_r, not_1_out;

  mux_1x2 mux_1x2_1 (.R(mux_1x2_1_r), .A(A0), .B(A1), .S(S0));
  mux_1x2 mux_1x2_2 (.R(mux_1x2_2_r), .A(A2), .B(A3), .S(S0));
  not not_1 (not_1_out, S1);
  and and_1 (and_1_out, mux_1x2_1_r, not_1_out);
  and and_2 (and_2_out, mux_1x2_2_r, S1);
  or or_1 (X, and_1_out, and_2_out);
endmodule
