// Logisim project somador_completo.circ as structural Verilog: 2 circuits, main circuit full_adder
module full_adder (
  input  Cin,
  input  A,
  input  B,
  output Cout,
  output S
);

  wire and_1_out, and_2_out, xor_1_out;

  and and_1 (and_1_out, A, B);
  xor xor_1 (xor_1_out, A, B);
  xor xor_2 (S, Cin, xor_1_out);
  and and_2 (and_2_out, Cin, xor_1_out);
  or or_1 (Cout, and_1_out, and_2_out);
endmodule

module somador_subtrator (
  input  M,
  input  A3,
  input  A2,
  input  A1,
  input  A0,
  input  B3,
  input  B2,
  input  B1,
  input  B0,
  output out_10,
  output out_11,
  output out_12,
  output out_13,
  output OVFL,
  output Cout
);

  wire and_1_out, and_2_out, and_3_out, and_4_out, and_5_out, and_6_out, and_7_out, and_8_out, and_9_out,
       and_10_out, G0_out, G1_out, G2_out, G3_out, or_1_out, or_2_out, or_3_out, P0_out, P1_out, P2_out,
       P3_out, xor_1_out, xor_2_out, xor_3_out, xor_4_out;

  xor xor_1 (xor_1_out, M, B3);
  xor xor_2 (xor_2_out, M, B0);
  xor xor_3 (xor_3_out, M, B1);
  xor xor_4 (xor_4_out, M, B2);
  and G1 (G1_out, xor_3_out, A1);
  or P1 (P1_out, xor_3_out, A1);
  and G0 (G0_out, A0, xor_2_out);
  or P0 (P0_out, A0, xor_2_out);
  and G2 (G2_out, xor_4_out, A2);
  or P2 (P2_out, xor_4_out, A2);
  and G3 (G3_out, xor_1_out, A3);
  or P3 (P3_out, xor_1_out, A3);
  and and_1 (and_1_out, P0_out, M);
  and and_2 (and_2_out, G0_out, P1_out);
  and and_3 (and_3_out, P1_out, M, P0_out);
  or or_1 (or_1_out, and_1_out, G0_out);
  and and_4 (and_4_out, G1_out, P2_out);
  and and_5 (and_5_out, P2_out, P1_out, G0_out);
  and and_6 (and_6_out, P2_out, P1_out, P0_out, M);
  and and_7 (and_7_out, P3_out, G2_out);
  and and_8 (and_8_out, P3_out, P2_out, G1_out);
  and and_9 (and_9_out, P3_out, P2_out, P1_out, G0_out);
  and and_10 (and_10_out, P3_out, P2_out, P1_out, P0_out, M);
  or or_2 (or_2_out, G1_out, and_2_out, and_3_out);
  or or_3 (or_3_out, G2_out, and_4_out, and_5_out, and_6_out);
  or or_4 (Cout, G3_out, and_7_out, and_8_out, and_9_out, and_10_out);
  full_adder full_adder_1 (.Cin(M), .A(A0), .B(xor_2_out), .S(out_13));  // open: Cout
  full_adder full_adder_2 (.Cin(or_1_out), .A(A1), .B(xor_3_out), .S(out_12));  // open: Cout
  full_adder full_adder_3 (.Cin(or_2_out), .A(A2), .B(xor_4_out), .S(out_11));  // open: Cout
  full_adder full_adder_4 (.Cin(or_3_out), .A(A3), .B(xor_1_out), .S(out_10));  // open: Cout
  xor xor_5 (OVFL, or_3_out, Cout);
endmodule
